// Logisim project 4bit_Binary_Counter_Project.circ as structural Verilog: 6 circuits, main circuit main
module main (
  output out_1,
  output out_2,
  output out_3,
  output out_4,
  output [6:0] out_5
);

  wire clock_1_out, clock_divider_1_divided_clock;
  wire [3:0] four_bit_counter_1_count1;
  wire [6:0] full_driver_1_digit_0, full_driver_1_digit_1, full_driver_1_digit_2, full_driver_1_digit_3;

  Clock clock_1 (.out(clock_1_out));
  clock_divider clock_divider_1 (.Clock(clock_1_out), .Divided_Clock(clock_divider_1_divided_clock));
  four_bit_counter four_bit_counter_1 (
    .Clock(clock_1_out), .Enable(clock_divider_1_divided_clock), .Count1(four_bit_counter_1_count1));
  full_driver full_driver_1 (
    .in_1(four_bit_counter_1_count1), .Digit_0(full_driver_1_digit_0), .Digit_1(full_driver_1_digit_1),
    .Digit_2(full_driver_1_digit_2), .Digit_3(full_driver_1_digit_3));
  display_selector display_selector_1 (
    .Clock(clock_1_out), .Display_1(full_driver_1_digit_0), .Display_2(full_driver_1_digit_1),
    .Display_3(full_driver_1_digit_2), .Display_4(full_driver_1_digit_3), .Display_1_Out(out_1),
    .Display_2_Out(out_2), .Display_3_Out(out_3), .Display_4_Out(out_4), .Display_Out(out_5));
endmodule

module clock_divider (
  input  Clock,
  output Divided_Clock
);

  wire not_1_out;
  wire [7:0] counter_1_q;

  Counter counter_1 (
    .load(Divided_Clock), .D(8'h6d), .count(1'b1), .Q(counter_1_q), .up(1'b1), .clk(Clock), .clr(1'b0));  // open: carry
  not not_1 (not_1_out, counter_1_q[7]);
  and and_1 (Divided_Clock, not_1_out, counter_1_q[6], counter_1_q[5], counter_1_q[4], counter_1_q[3], counter_1_q[2], counter_1_q[1], counter_1_q[0]);
endmodule

module four_bit_counter (
  input  Clock,
  input  Enable,
  output [3:0] Count1
);

  Counter #(.max('hf), .width(4)) counter_1 (
    .load(1'b0), .count(Enable), .Q(Count1), .up(1'b1), .clk(Clock), .clr(1'b0));  // open: D, carry
endmodule

module driver (
  input  Digit,
  output [6:0] out_2
);

  not not_1 (out_2[5], Digit);

  assign {out_2[6], out_2[4:0]} = {1'b0, {2{out_2[5]}}, 2'b11, out_2[5]};
endmodule

module full_driver (
  input  [3:0] in_1,
  output [6:0] Digit_0,
  output [6:0] Digit_1,
  output [6:0] Digit_2,
  output [6:0] Digit_3
);

  driver driver_1 (.Digit(in_1[0]), .out_2(Digit_0));
  driver driver_2 (.Digit(in_1[1]), .out_2(Digit_1));
  driver driver_3 (.Digit(in_1[2]), .out_2(Digit_2));
  driver driver_4 (.Digit(in_1[3]), .out_2(Digit_3));
endmodule

module display_selector (
  input  Clock,
  input  [6:0] Display_1,
  input  [6:0] Display_2,
  input  [6:0] Display_3,
  input  [6:0] Display_4,
  output Display_1_Out,
  output Display_2_Out,
  output Display_3_Out,
  output Display_4_Out,
  output [6:0] Display_Out
);

  wire [1:0] counter_1_q;

  Counter #(.max('h3), .width(2)) counter_1 (
    .load(1'b0), .count(1'b1), .Q(counter_1_q), .up(1'b1), .clk(Clock), .clr(1'b0));  // open: D, carry
  Demultiplexer #(.enable("true"), .select(2)) demultiplexer_1 (
    .out0(Display_1_Out), .out1(Display_2_Out), .out2(Display_3_Out), .out3(Display_4_Out), .in(1'b1),
    .sel(counter_1_q), .en(1'b1));
  Multiplexer #(.select(2), .width(7)) multiplexer_1 (
    .in0(Display_1), .in1(Display_2), .in2(Display_3), .in3(Display_4), .out(Display_Out), .sel(counter_1_q));
endmodule
