// Logisim project 60Second_Timer.circ as structural Verilog: 7 circuits, main circuit main
module main (
  input  Decrement,
  input  Start_Stop,
  input  Speed_4x,
  output Display1_Out,
  output Display2_Out,
  output Display3_Out,
  output [6:0] DisplaySSD_Out,
  output Display4_Out
);

  wire clock_1_out, clock_divider_1_divided_clock, digit_one_counter_1_carry_out,
       digit_zero_counter_1_carry_out;
  wire [3:0] digit_one_counter_1_count1, digit_zero_counter_1_count1, digit_zero_counter_2_count1;
  wire [6:0] full_driver_1_d0_ssd, full_driver_1_d1_ssd, full_driver_1_d2_ssd;

  Clock clock_1 (.out(clock_1_out));
  clock_divider clock_divider_1 (
    .Clock(clock_1_out), .Speed_4x(Speed_4x), .Divided_Clock(clock_divider_1_divided_clock));
  digit_zero_counter digit_zero_counter_1 (
    .Decrement(Decrement), .Clock(clock_1_out), .Enable_Clock(clock_divider_1_divided_clock),
    .Start_Stop(Start_Stop), .Count1(digit_zero_counter_1_count1), .Carry_Out(digit_zero_counter_1_carry_out));
  digit_one_counter digit_one_counter_1 (
    .Decrement(Decrement), .Clock(clock_1_out), .Enable_Clock(digit_zero_counter_1_carry_out),
    .Start_Stop(Start_Stop), .Count1(digit_one_counter_1_count1), .Carry_Out(digit_one_counter_1_carry_out));
  digit_zero_counter digit_zero_counter_2 (
    .Decrement(Decrement), .Clock(clock_1_out), .Enable_Clock(digit_one_counter_1_carry_out),
    .Start_Stop(Start_Stop), .Count1(digit_zero_counter_2_count1));  // open: Carry_Out
  full_driver full_driver_1 (
    .D0(digit_zero_counter_1_count1), .D1(digit_one_counter_1_count1), .D2(digit_zero_counter_2_count1),
    .D0_SSD(full_driver_1_d0_ssd), .D1_SSD(full_driver_1_d1_ssd), .D2_SSD(full_driver_1_d2_ssd));
  mux_demux mux_demux_1 (
    .Clock(clock_1_out), .Display_1(full_driver_1_d0_ssd), .Display_2(full_driver_1_d1_ssd),
    .Display_3(full_driver_1_d2_ssd), .Display_1_Out(Display1_Out), .Display_2_Out(Display2_Out),
    .Display_3_Out(Display3_Out), .Display_Out(DisplaySSD_Out));

  assign Display4_Out = 1'b0;
endmodule

module clock_divider (
  input  Clock,
  input  Speed_4x,
  output Divided_Clock
);

  wire and_1_out, and_2_out, not_1_out, not_2_out;
  wire [8:0] counter_1_q;

  Counter #(.max('h1ff), .width(9)) counter_1 (
    .load(Divided_Clock), .D({9{1'b0}}), .count(1'b1), .Q(counter_1_q), .up(1'b1), .clk(Clock), .clr(1'b0));  // open: carry
  and and_1 (and_1_out, counter_1_q[8], counter_1_q[7], counter_1_q[6], counter_1_q[5], counter_1_q[4], counter_1_q[3], counter_1_q[2], counter_1_q[1], counter_1_q[0]);
  not not_1 (not_1_out, counter_1_q[8]);
  Multiplexer multiplexer_1 (.in0(and_1_out), .in1(and_2_out), .out(Divided_Clock), .sel(Speed_4x));
  not not_2 (not_2_out, counter_1_q[7]);
  and and_2 (and_2_out, not_1_out, not_2_out, counter_1_q[6], counter_1_q[5], counter_1_q[4], counter_1_q[3], counter_1_q[2], counter_1_q[1], counter_1_q[0]);
endmodule

module digit_zero_counter (
  input  Decrement,
  input  Clock,
  input  Enable_Clock,
  input  Start_Stop,
  output [3:0] Count1,
  output Carry_Out
);

  wire and_1_out, and_3_out, and_4_out, multiplexer_2_out, not_1_out, not_2_out, not_3_out, not_4_out,
       not_5_out, not_6_out, not_7_out, not_8_out;
  wire [3:0] multiplexer_1_out;

  not not_1 (not_1_out, Decrement);
  not not_2 (not_2_out, Start_Stop);
  Multiplexer #(.width(4)) multiplexer_1 (.in0(4'b0000), .in1(4'b1001), .out(multiplexer_1_out), .sel(Decrement));
  and and_1 (and_1_out, Enable_Clock, not_2_out);
  Counter #(.max('hf), .width(4)) counter_1 (
    .load(Carry_Out), .D(multiplexer_1_out), .count(and_1_out), .Q(Count1), .up(not_1_out), .clk(Clock),
    .clr(1'b0));  // open: carry
  and and_2 (Carry_Out, and_1_out, multiplexer_2_out);
  not not_3 (not_3_out, Count1[3]);
  not not_4 (not_4_out, Count1[2]);
  not not_5 (not_5_out, Count1[1]);
  not not_6 (not_6_out, Count1[0]);
  and and_3 (and_3_out, not_3_out, not_4_out, not_5_out, not_6_out);
  not not_7 (not_7_out, Count1[2]);
  not not_8 (not_8_out, Count1[1]);
  and and_4 (and_4_out, Count1[3], not_7_out, not_8_out, Count1[0]);
  Multiplexer multiplexer_2 (.in0(and_4_out), .in1(and_3_out), .out(multiplexer_2_out), .sel(Decrement));
endmodule

module digit_one_counter (
  input  Decrement,
  input  Clock,
  input  Enable_Clock,
  input  Start_Stop,
  output [3:0] Count1,
  output Carry_Out
);

  wire and_1_out, and_3_out, and_4_out, multiplexer_2_out, not_1_out, not_2_out, not_3_out, not_4_out,
       not_5_out, not_6_out, not_7_out, not_8_out;
  wire [3:0] multiplexer_1_out;

  not not_1 (not_1_out, Start_Stop);
  not not_2 (not_2_out, Decrement);
  Multiplexer #(.width(4)) multiplexer_1 (.in0(4'b0000), .in1(4'b0101), .out(multiplexer_1_out), .sel(Decrement));
  and and_1 (and_1_out, Enable_Clock, not_1_out);
  Counter #(.max('hf), .width(4)) counter_1 (
    .load(Carry_Out), .D(multiplexer_1_out), .count(and_1_out), .Q(Count1), .up(not_2_out), .clk(Clock),
    .clr(1'b0));  // open: carry
  and and_2 (Carry_Out, and_1_out, multiplexer_2_out);
  not not_3 (not_3_out, Count1[3]);
  not not_4 (not_4_out, Count1[2]);
  not not_5 (not_5_out, Count1[1]);
  and and_3 (and_3_out, not_3_out, not_4_out, not_5_out, not_6_out);
  not not_6 (not_6_out, Count1[0]);
  not not_7 (not_7_out, Count1[3]);
  and and_4 (and_4_out, not_7_out, Count1[2], not_8_out, Count1[0]);
  Multiplexer multiplexer_2 (.in0(and_4_out), .in1(and_3_out), .out(multiplexer_2_out), .sel(Decrement));
  not not_8 (not_8_out, Count1[1]);
endmodule

module driver (
  input  [3:0] Digit,
  output [6:0] Output_bus_1
);

  wire n7447_1_pin3;

  _7447 #(.ShowInternalStructure("true")) u_7447_1 (
    .pin1(Digit[1]), .pin2(Digit[2]), .pin3(n7447_1_pin3), .pin4(n7447_1_pin3), .pin5(n7447_1_pin3),
    .pin6(Digit[3]), .pin7(Digit[0]), .pin15(Output_bus_1[5]), .pin14(Output_bus_1[6]),
    .pin13(Output_bus_1[0]), .pin12(Output_bus_1[1]), .pin11(Output_bus_1[2]), .pin10(Output_bus_1[3]),
    .pin9(Output_bus_1[4]));
  // also tied to VCC on the sheet: n7447_1_pin3
endmodule

module full_driver (
  input  [3:0] D0,
  input  [3:0] D1,
  input  [3:0] D2,
  output [6:0] D0_SSD,
  output [6:0] D1_SSD,
  output [6:0] D2_SSD
);

  driver driver_1 (.Digit(D0), .Output_bus_1(D0_SSD));
  driver driver_2 (.Digit(D1), .Output_bus_1(D1_SSD));
  driver driver_3 (.Digit(D2), .Output_bus_1(D2_SSD));
endmodule

module mux_demux (
  input  Clock,
  input  [6:0] Display_1,
  input  [6:0] Display_2,
  input  [6:0] Display_3,
  output Display_1_Out,
  output Display_2_Out,
  output Display_3_Out,
  output [6:0] Display_Out
);

  wire [1:0] counter_1_q;

  Counter #(.max('h3), .width(2)) counter_1 (
    .load(1'b0), .count(1'b1), .Q(counter_1_q), .up(1'b1), .clk(Clock), .clr(1'b0));  // open: D, carry
  Demultiplexer #(.enable("true"), .select(2)) demultiplexer_1 (
    .out0(Display_1_Out), .out1(Display_2_Out), .out2(Display_3_Out), .in(1'b1), .sel(counter_1_q), .en(1'b1));  // open: out3
  Multiplexer #(.select(2), .width(7)) multiplexer_1 (
    .in0(Display_1), .in1(Display_2), .in2(Display_3), .in3({7{1'b0}}), .out(Display_Out), .sel(counter_1_q));
endmodule
