// Logisim project 8_bit_adder.circ as structural Verilog: 2 circuits, main circuit Inverter
module main (
  input  ASign,
  input  [7:0] A,
  input  BSign,
  input  [7:0] B
);

  wire adder_1_cout, adder_2_cout, adder_3_cout, adder_4_cout, adder_5_cout, adder_6_cout, adder_7_cout,
       n7447_1_pin3, n7447_1_pin9, n7447_1_pin10, n7447_1_pin11, n7447_1_pin12, n7447_1_pin13, n7447_1_pin14,
       n7447_1_pin15;
  wire [7:0] adder_1_out, inverter_1_out_3, inverter_2_out_3, inverter_3_out_3;

  Inverter inverter_1 (.Sign(ASign), .Value(A), .out_3(inverter_1_out_3));
  Inverter inverter_2 (.Sign(BSign), .Value(B), .out_3(inverter_2_out_3));
  Adder #(.width(1)) adder_1 (
    .a(inverter_1_out_3[0]), .b(inverter_2_out_3[0]), .out(adder_1_out[0]), .cin(1'b0), .cout(adder_1_cout));
  Adder #(.width(1)) adder_2 (
    .a(inverter_1_out_3[1]), .b(inverter_2_out_3[1]), .out(adder_1_out[1]), .cin(adder_1_cout),
    .cout(adder_2_cout));
  Adder #(.width(1)) adder_3 (
    .a(inverter_1_out_3[2]), .b(inverter_2_out_3[2]), .out(adder_1_out[2]), .cin(adder_2_cout),
    .cout(adder_3_cout));
  Adder #(.width(1)) adder_4 (
    .a(inverter_1_out_3[3]), .b(inverter_2_out_3[3]), .out(adder_1_out[3]), .cin(adder_3_cout),
    .cout(adder_4_cout));
  Adder #(.width(1)) adder_5 (
    .a(inverter_1_out_3[4]), .b(inverter_2_out_3[4]), .out(adder_1_out[4]), .cin(adder_4_cout),
    .cout(adder_5_cout));
  Adder #(.width(1)) adder_6 (
    .a(inverter_1_out_3[5]), .b(inverter_2_out_3[5]), .out(adder_1_out[5]), .cin(adder_5_cout),
    .cout(adder_6_cout));
  Adder #(.width(1)) adder_7 (
    .a(inverter_1_out_3[6]), .b(inverter_2_out_3[6]), .out(adder_1_out[6]), .cin(adder_6_cout),
    .cout(adder_7_cout));
  Adder #(.width(1)) adder_8 (
    .a(inverter_1_out_3[7]), .b(inverter_2_out_3[7]), .out(adder_1_out[7]), .cin(adder_7_cout));  // open: cout
  LED led_1 (.in(adder_1_out[7]));
  LED led_2 (.in(adder_1_out[6]));
  LED led_3 (.in(adder_1_out[5]));
  LED led_4 (.in(adder_1_out[4]));
  LED led_5 (.in(adder_1_out[3]));
  LED led_6 (.in(adder_1_out[2]));
  LED led_7 (.in(adder_1_out[1]));
  LED led_8 (.in(adder_1_out[0]));
  Inverter inverter_3 (.Sign(adder_1_out[7]), .Value(adder_1_out), .out_3(inverter_3_out_3));
  _7447 #(.ShowInternalStructure("true")) u_7447_1 (
    .pin1(inverter_3_out_3[1]), .pin2(inverter_3_out_3[2]), .pin3(n7447_1_pin3), .pin4(n7447_1_pin3),
    .pin5(n7447_1_pin3), .pin6(inverter_3_out_3[0]), .pin7(inverter_3_out_3[3]), .pin15(n7447_1_pin15),
    .pin14(n7447_1_pin14), .pin13(n7447_1_pin13), .pin12(n7447_1_pin12), .pin11(n7447_1_pin11),
    .pin10(n7447_1_pin10), .pin9(n7447_1_pin9));
  _7_Segment_Display #(.decimalPoint("false")) u_7_segment_display_1 (.g(adder_1_out[7]));  // open: f, a, b, e, d, c
  _7_Segment_Display #(.active("false"), .decimalPoint("false")) u_7_segment_display_2 (
    .g(n7447_1_pin14), .f(n7447_1_pin15), .a(n7447_1_pin13), .b(n7447_1_pin12), .e(n7447_1_pin9),
    .d(n7447_1_pin10), .c(n7447_1_pin11));
  // also tied to VCC on the sheet: n7447_1_pin3
endmodule

module Inverter (
  input  Sign,
  input  [7:0] Value,
  output [7:0] out_3
);

  wire adder_1_cout, adder_2_cout, adder_3_cout, adder_4_cout, adder_5_cout, adder_6_cout, adder_7_cout,
       xor_1_out, xor_2_out, xor_3_out, xor_4_out, xor_5_out, xor_6_out, xor_7_out, xor_8_out;

  xor xor_1 (xor_1_out, Sign, Value[0]);
  xor xor_2 (xor_2_out, Sign, Value[1]);
  xor xor_3 (xor_3_out, Sign, Value[2]);
  xor xor_4 (xor_4_out, Sign, Value[3]);
  xor xor_5 (xor_5_out, Sign, Value[4]);
  xor xor_6 (xor_6_out, Sign, Value[5]);
  xor xor_7 (xor_7_out, Sign, Value[6]);
  xor xor_8 (xor_8_out, Sign, Value[7]);
  Adder #(.width(1)) adder_1 (.a(xor_1_out), .b(1'b0), .out(out_3[0]), .cin(Sign), .cout(adder_1_cout));
  Adder #(.width(1)) adder_2 (.a(xor_2_out), .b(1'b0), .out(out_3[1]), .cin(adder_1_cout), .cout(adder_2_cout));
  Adder #(.width(1)) adder_3 (.a(xor_3_out), .b(1'b0), .out(out_3[2]), .cin(adder_2_cout), .cout(adder_3_cout));
  Adder #(.width(1)) adder_4 (.a(xor_4_out), .b(1'b0), .out(out_3[3]), .cin(adder_3_cout), .cout(adder_4_cout));
  Adder #(.width(1)) adder_5 (.a(xor_5_out), .b(1'b0), .out(out_3[4]), .cin(adder_4_cout), .cout(adder_5_cout));
  Adder #(.width(1)) adder_6 (.a(xor_6_out), .b(1'b0), .out(out_3[5]), .cin(adder_5_cout), .cout(adder_6_cout));
  Adder #(.width(1)) adder_7 (.a(xor_7_out), .b(1'b0), .out(out_3[6]), .cin(adder_6_cout), .cout(adder_7_cout));
  Adder #(.width(1)) adder_8 (.a(xor_8_out), .b(1'b0), .out(out_3[7]), .cin(adder_7_cout));  // open: cout
endmodule
