// Logisim project Binary_Adder.circ as structural Verilog: 1 circuit, main circuit main
module main (
  input  X0,
  input  Y0,
  input  X1,
  input  Y1,
  input  X2,
  input  Y2,
  input  X3,
  input  Y3
);

  wire and_1_out, and_2_out, and_3_out, and_4_out, and_5_out, and_6_out, and_7_out, and_8_out, and_9_out,
       and_10_out, n7447_1_pin1, n7447_1_pin3, n7447_1_pin9, n7447_1_pin10, n7447_1_pin11, n7447_1_pin12,
       n7447_1_pin13, n7447_1_pin14, n7447_1_pin15, n7447_2_pin9, n7447_2_pin10, n7447_2_pin11,
       n7447_2_pin12, n7447_2_pin13, n7447_2_pin14, n7447_2_pin15, or_1_out, or_2_out, or_3_out, or_4_out,
       or_5_out, or_6_out, xor_1_out, xor_2_out, xor_3_out, xor_4_out, xor_5_out, xor_6_out, xor_7_out;

  and and_1 (and_1_out, X0, Y0);
  xor xor_1 (xor_1_out, X0, Y0);
  xor xor_2 (xor_2_out, X1, Y1);
  and and_2 (and_2_out, and_1_out, Y1);
  and and_3 (and_3_out, and_1_out, X1);
  and and_4 (and_4_out, Y1, X1);
  xor xor_3 (xor_3_out, X2, Y2);
  and and_5 (and_5_out, or_4_out, Y2);
  and and_6 (and_6_out, or_4_out, X2);
  and and_7 (and_7_out, Y2, X2);
  xor xor_4 (xor_4_out, X3, Y3);
  and and_8 (and_8_out, or_5_out, Y3);
  and and_9 (and_9_out, or_5_out, X3);
  and and_10 (and_10_out, Y3, X3);
  xor xor_5 (xor_5_out, or_4_out, xor_3_out);
  xor xor_6 (xor_6_out, or_5_out, xor_4_out);
  xor xor_7 (xor_7_out, and_1_out, xor_2_out);
  or or_1 (or_1_out, and_2_out, and_3_out);
  or or_2 (or_2_out, and_5_out, and_6_out);
  or or_3 (or_3_out, and_8_out, and_9_out);
  or or_4 (or_4_out, or_1_out, and_4_out);
  or or_5 (or_5_out, or_2_out, and_7_out);
  or or_6 (or_6_out, or_3_out, and_10_out);
  LED S4 (.in(or_6_out));
  LED S3 (.in(xor_6_out));
  LED S2 (.in(xor_5_out));
  LED S1 (.in(xor_7_out));
  LED S0 (.in(xor_1_out));
  _7447 #(.ShowInternalStructure("true")) u_7447_1 (
    .pin1(n7447_1_pin1), .pin2(n7447_1_pin1), .pin3(n7447_1_pin3), .pin4(n7447_1_pin3), .pin5(n7447_1_pin3),
    .pin6(n7447_1_pin1), .pin7(or_6_out), .pin15(n7447_1_pin15), .pin14(n7447_1_pin14),
    .pin13(n7447_1_pin13), .pin12(n7447_1_pin12), .pin11(n7447_1_pin11), .pin10(n7447_1_pin10),
    .pin9(n7447_1_pin9));
  _7447 #(.ShowInternalStructure("true")) u_7447_2 (
    .pin1(xor_7_out), .pin2(xor_5_out), .pin3(n7447_1_pin3), .pin4(n7447_1_pin3), .pin5(n7447_1_pin3),
    .pin6(xor_6_out), .pin7(xor_1_out), .pin15(n7447_2_pin15), .pin14(n7447_2_pin14), .pin13(n7447_2_pin13),
    .pin12(n7447_2_pin12), .pin11(n7447_2_pin11), .pin10(n7447_2_pin10), .pin9(n7447_2_pin9));
  _7_Segment_Display #(.active("false"), .decimalPoint("false")) u_7_segment_display_1 (
    .g(n7447_1_pin14), .f(n7447_1_pin15), .a(n7447_1_pin13), .b(n7447_1_pin12), .e(n7447_1_pin9),
    .d(n7447_1_pin10), .c(n7447_1_pin11));
  _7_Segment_Display #(.active("false"), .decimalPoint("false")) u_7_segment_display_2 (
    .g(n7447_2_pin14), .f(n7447_2_pin15), .a(n7447_2_pin13), .b(n7447_2_pin12), .e(n7447_2_pin9),
    .d(n7447_2_pin10), .c(n7447_2_pin11));
  // also tied to GND on the sheet: n7447_1_pin1
  // also tied to VCC on the sheet: n7447_1_pin3
endmodule
