// Logisim project Binary_Adder_Simplified.circ as structural Verilog: 1 circuit, main circuit main
module main (
);

  wire adder_1_cout, adder_1_out, adder_2_cout, adder_2_out, adder_3_cout, adder_3_out, adder_4_cout,
       adder_4_out, n7447_1_pin1, n7447_1_pin3, n7447_1_pin9, n7447_1_pin10, n7447_1_pin11, n7447_1_pin12,
       n7447_1_pin13, n7447_1_pin14, n7447_1_pin15, n7447_2_pin9, n7447_2_pin10, n7447_2_pin11,
       n7447_2_pin12, n7447_2_pin13, n7447_2_pin14, n7447_2_pin15;
  wire [3:0] dipswitch_1_sw4, dipswitch_2_sw4;

  DipSwitch #(.number(4)) dipswitch_1 (
    .sw1(dipswitch_1_sw4[3]), .sw2(dipswitch_1_sw4[2]), .sw3(dipswitch_1_sw4[1]), .sw4(dipswitch_1_sw4[0]));
  DipSwitch #(.number(4)) dipswitch_2 (
    .sw1(dipswitch_2_sw4[3]), .sw2(dipswitch_2_sw4[2]), .sw3(dipswitch_2_sw4[1]), .sw4(dipswitch_2_sw4[0]));
  Adder #(.width(1)) adder_1 (
    .a(dipswitch_1_sw4[0]), .b(dipswitch_2_sw4[0]), .out(adder_1_out), .cin(1'b0), .cout(adder_1_cout));
  Adder #(.width(1)) adder_2 (
    .a(dipswitch_1_sw4[1]), .b(dipswitch_2_sw4[1]), .out(adder_2_out), .cin(adder_1_cout), .cout(adder_2_cout));
  Adder #(.width(1)) adder_3 (
    .a(dipswitch_1_sw4[2]), .b(dipswitch_2_sw4[2]), .out(adder_3_out), .cin(adder_2_cout), .cout(adder_3_cout));
  Adder #(.width(1)) adder_4 (
    .a(dipswitch_1_sw4[3]), .b(dipswitch_2_sw4[3]), .out(adder_4_out), .cin(adder_3_cout), .cout(adder_4_cout));
  _7447 #(.ShowInternalStructure("true")) u_7447_1 (
    .pin1(n7447_1_pin1), .pin2(n7447_1_pin1), .pin3(n7447_1_pin3), .pin4(n7447_1_pin3), .pin5(n7447_1_pin3),
    .pin6(n7447_1_pin1), .pin7(adder_4_cout), .pin15(n7447_1_pin15), .pin14(n7447_1_pin14),
    .pin13(n7447_1_pin13), .pin12(n7447_1_pin12), .pin11(n7447_1_pin11), .pin10(n7447_1_pin10),
    .pin9(n7447_1_pin9));
  _7447 #(.ShowInternalStructure("true")) u_7447_2 (
    .pin1(adder_2_out), .pin2(adder_3_out), .pin3(n7447_1_pin3), .pin4(n7447_1_pin3), .pin5(n7447_1_pin3),
    .pin6(adder_4_out), .pin7(adder_1_out), .pin15(n7447_2_pin15), .pin14(n7447_2_pin14),
    .pin13(n7447_2_pin13), .pin12(n7447_2_pin12), .pin11(n7447_2_pin11), .pin10(n7447_2_pin10),
    .pin9(n7447_2_pin9));
  _7_Segment_Display #(.active("false"), .decimalPoint("false")) u_7_segment_display_1 (
    .g(n7447_1_pin14), .f(n7447_1_pin15), .a(n7447_1_pin13), .b(n7447_1_pin12), .e(n7447_1_pin9),
    .d(n7447_1_pin10), .c(n7447_1_pin11));
  _7_Segment_Display #(.active("false"), .decimalPoint("false")) u_7_segment_display_2 (
    .g(n7447_2_pin14), .f(n7447_2_pin15), .a(n7447_2_pin13), .b(n7447_2_pin12), .e(n7447_2_pin9),
    .d(n7447_2_pin10), .c(n7447_2_pin11));
  // also tied to GND on the sheet: n7447_1_pin1
  // also tied to VCC on the sheet: n7447_1_pin3
endmodule
