// Logisim project DFF_practice.circ as structural Verilog: 1 circuit, main circuit main
module main (
  output out_1,
  output out_2
);

  wire clock_1_out, clock_2_out, clock_3_out, d_ff_1_q, d_ff_2_q, d_ff_2_qn, d_ff_3_q, d_ff_3_qn, d_ff_5_qn,
       xor_1_out, xor_2_out;

  Clock clock_1 (.out(clock_1_out));
  D_Flip_Flop d_ff_1 (.D(xor_1_out), .clk(clock_1_out), .Q(d_ff_1_q));  // open: Qn, preset, reset
  xor xor_1 (xor_1_out, d_ff_1_q, d_ff_3_q);
  Clock clock_2 (.out(clock_2_out));
  D_Flip_Flop d_ff_2 (.D(d_ff_2_qn), .clk(clock_2_out), .Q(d_ff_2_q), .Qn(d_ff_2_qn));  // open: preset, reset
  D_Flip_Flop d_ff_3 (.D(d_ff_3_qn), .clk(clock_1_out), .Q(d_ff_3_q), .Qn(d_ff_3_qn));  // open: preset, reset
  // Digital_Oscilloscope digital_oscilloscope_1: pin names not known; wires that end beside it: clock_2_out, d_ff_2_q
  // Digital_Oscilloscope digital_oscilloscope_2: pin names not known; wires that end beside it: clock_1_out, d_ff_1_q
  Clock clock_3 (.out(clock_3_out));
  xor xor_2 (xor_2_out, out_2, out_1);
  D_Flip_Flop d_ff_4 (.D(xor_2_out), .clk(clock_3_out), .Q(out_2));  // open: Qn, preset, reset
  D_Flip_Flop d_ff_5 (.D(d_ff_5_qn), .clk(clock_3_out), .Q(out_1), .Qn(d_ff_5_qn));  // open: preset, reset
endmodule
