// Logisim project DeMorgan_Assignments.circ as structural Verilog: 1 circuit, main circuit main
module main (
  input  [2:0] in_1,
  output out_2
);

  wire and_1_out, and_2_out, and_3_out, and_4_out, dipswitch_1_sw1, dipswitch_1_sw2, dipswitch_1_sw3,
       nand_1_out, nand_2_out, nand_3_out, nand_4_out, nand_5_out, nand_6_out, nand_7_out, nand_8_out,
       nand_9_out, nand_10_out, nand_11_out, not_1_out, not_2_out, not_3_out, or_1_out;

  DipSwitch #(.number(3)) dipswitch_1 (.sw1(dipswitch_1_sw1), .sw2(dipswitch_1_sw2), .sw3(dipswitch_1_sw3));
  nand nand_1 (nand_1_out, dipswitch_1_sw1, dipswitch_1_sw1);
  not not_1 (not_1_out, in_1[2]);
  not not_2 (not_2_out, in_1[0]);
  not not_3 (not_3_out, in_1[1]);
  nand nand_2 (nand_2_out, dipswitch_1_sw2, nand_1_out);
  nand nand_3 (nand_3_out, dipswitch_1_sw3, dipswitch_1_sw3);
  nand nand_4 (nand_4_out, dipswitch_1_sw2, dipswitch_1_sw2);
  and and_1 (and_1_out, in_1[1], not_1_out);
  and and_2 (and_2_out, not_3_out, in_1[2]);
  and and_3 (and_3_out, in_1[0], in_1[2]);
  nand nand_5 (nand_5_out, nand_2_out, nand_2_out);
  nand nand_6 (nand_6_out, dipswitch_1_sw3, dipswitch_1_sw1);
  and and_4 (and_4_out, and_1_out, not_2_out);
  or or_1 (or_1_out, and_2_out, and_3_out);
  nand nand_7 (nand_7_out, nand_5_out, nand_3_out);
  nand nand_8 (nand_8_out, nand_4_out, dipswitch_1_sw1);
  or or_2 (out_2, and_4_out, or_1_out);
  nand nand_9 (nand_9_out, nand_8_out, nand_6_out);
  nand nand_10 (nand_10_out, nand_9_out, nand_9_out);
  nand nand_11 (nand_11_out, nand_7_out, nand_10_out);
  LED led_1 (.in(nand_11_out));
endmodule
