// Logisim project Final_Project (Hamming Encoder & Decoder + CRC Generator & Decoder).circ as structural Verilog: 5 circuits, main circuit main
module main (
  input  Input_1,
  input  Input_2,
  input  Input_3,
  input  Input_4,
  input  Input_5,
  input  Input_6,
  input  Input_7,
  input  Input_8,
  input  Input_9,
  input  Input_10,
  input  Input_11,
  input  Input_12,
  input  Input_13,
  input  Input_14,
  input  Input_15,
  input  Input_16,
  input  Input_17,
  input  Input_18,
  input  Input_19,
  input  Input_20,
  input  Input_21,
  input  Input_22,
  input  Input_23,
  input  Input_24,
  input  Input_25,
  output Output_1,
  output Output_2,
  output Output_3,
  output Output_4,
  output [11:0] Output_bus_1,
  output Output_5,
  output Output_6,
  output Output_7,
  output Output_8,
  output Output_9,
  output Output_10,
  output Output_11,
  output Output_12,
  output Output_13,
  output Output_14,
  output Output_15,
  output Output_16,
  output Output_17,
  output Output_18,
  output Output_19,
  output Output_20,
  output Output_21,
  output Output_22,
  output Output_23,
  output Output_24,
  output Output_25,
  output Output_26,
  output Output_27,
  output Output_28,
  output Output_29,
  output Output_30,
  output Output_31,
  output Output_32,
  output Output_33,
  output Output_34,
  output Output_35,
  output Output_36,
  output Output_37,
  output Output_38,
  output Output_39
);

  wire clock_1_out;

  Clock clock_1 (.out(clock_1_out));
  hamming_encoder hamming_encoder_1 (
    .Input_1(Input_1), .Input_2(Input_2), .Input_3(Input_3), .Input_4(Input_4), .Input_5(Input_5),
    .Input_6(Input_6), .Input_7(Input_7), .Input_8(Input_8),
    .Output_bus_1({Output_18, Output_19, Output_2, Output_20, Output_4, Output_6, Output_8, Output_21, Output_10, Output_12, Output_14, Output_16}),
    .Output_1(Output_22));
  crc_generator crc_generator_1 (
    .Input_1(Input_1), .Input_2(Input_2), .Input_3(Input_3), .Input_4(Input_4), .Input_5(Input_5),
    .Input_6(Input_6), .Input_7(Input_7), .Input_8(Input_8), .Clock(clock_1_out), .Output_1(Output_36),
    .Output_2(Output_37), .Output_3(Output_38), .Output_4(Output_39));
  crc_decoder crc_decoder_1 (
    .Input_1(Input_1), .Input_2(Input_2), .Input_3(Input_3), .Input_4(Input_4), .Input_5(Input_5),
    .Input_6(Input_6), .Input_7(Input_7), .Input_8(Input_8), .Input_9(Input_21), .Input_10(Input_19),
    .Input_11(Input_17), .Input_12(Input_15), .Clock(clock_1_out), .Output_1(Output_23),
    .Output_2(Output_25), .Output_3(Output_27), .Output_4(Output_29));
  hamming_decoder hamming_decoder_1 (
    .Input_1(Output_2), .Input_2(Output_4), .Input_3(Output_6), .Input_4(Output_8), .Input_5(Output_10),
    .Input_6(Output_12), .Input_7(Output_14), .Input_8(Output_16), .Input_9(Output_18), .Input_10(Output_19),
    .Input_11(Output_20), .Input_12(Output_21), .Input_13(Output_22), .Output_1(Output_1),
    .Output_2(Output_3), .Output_3(Output_5), .Output_4(Output_7), .Output_5(Output_9), .Output_6(Output_11),
    .Output_7(Output_13), .Output_8(Output_15), .Output_9(Output_17));
  hamming_decoder hamming_decoder_2 (
    .Input_1(Input_9), .Input_2(Input_10), .Input_3(Input_11), .Input_4(Input_12), .Input_5(Input_13),
    .Input_6(Input_14), .Input_7(Input_16), .Input_8(Input_18), .Input_9(Input_20), .Input_10(Input_22),
    .Input_11(Input_23), .Input_12(Input_24), .Input_13(Input_25), .Output_1(Output_24),
    .Output_2(Output_26), .Output_3(Output_28), .Output_4(Output_30), .Output_5(Output_31),
    .Output_6(Output_32), .Output_7(Output_33), .Output_8(Output_34), .Output_9(Output_35));

  assign Output_bus_1 = {Output_18, Output_19, Output_2, Output_20, Output_4, Output_6, Output_8, Output_21, Output_10, Output_12, Output_14, Output_16};
endmodule

module hamming_encoder (
  input  Input_1,
  input  Input_2,
  input  Input_3,
  input  Input_4,
  input  Input_5,
  input  Input_6,
  input  Input_7,
  input  Input_8,
  output [11:0] Output_bus_1,
  output Output_1
);

  xor xor_1 (Output_bus_1[11], Input_1, Input_2, Input_4, Input_5, Input_7);
  xor xor_2 (Output_bus_1[10], Input_1, Input_3, Input_4, Input_6, Input_7);
  xor xor_3 (Output_bus_1[8], Input_2, Input_3, Input_4, Input_8, 1'b0);
  xor xor_4 (Output_bus_1[4], Input_5, Input_6, Input_7, Input_8, 1'b0);
  xor xor_5 (Output_1, Output_bus_1[11], Output_bus_1[10], Output_bus_1[8], Output_bus_1[4], 1'b0);

  assign {Output_bus_1[9], Output_bus_1[7:5], Output_bus_1[3:0]} = {Input_1, Input_2, Input_3, Input_4, Input_5, Input_6, Input_7, Input_8};
endmodule

module hamming_decoder (
  input  Input_1,
  input  Input_2,
  input  Input_3,
  input  Input_4,
  input  Input_5,
  input  Input_6,
  input  Input_7,
  input  Input_8,
  input  Input_9,
  input  Input_10,
  input  Input_11,
  input  Input_12,
  input  Input_13,
  output Output_1,
  output Output_2,
  output Output_3,
  output Output_4,
  output Output_5,
  output Output_6,
  output Output_7,
  output Output_8,
  output Output_9
);

  wire and_1_out, and_2_out, and_3_out, and_4_out, and_5_out, and_6_out, and_7_out, and_8_out, not_1_out,
       not_2_out, not_3_out, not_4_out, not_5_out, not_6_out, not_7_out, not_8_out, not_9_out, not_10_out,
       not_11_out, not_12_out, not_13_out, not_14_out, not_15_out, not_16_out, not_17_out, not_18_out,
       xnor_1_out, xnor_2_out, xnor_3_out, xnor_4_out, xor_1_out, xor_2_out, xor_3_out, xor_4_out, xor_5_out;

  xor xor_1 (xor_1_out, Input_1, Input_5, Input_2, Input_7, Input_4);
  xor xor_2 (xor_2_out, Input_1, Input_6, Input_3, Input_7, Input_4);
  xor xor_3 (xor_3_out, Input_2, Input_8, Input_3, 1'b0, Input_4);
  xor xor_4 (xor_4_out, 1'b0, Input_5, Input_6, Input_7, Input_8);
  xor xor_5 (xor_5_out, Input_9, Input_10, Input_11, Input_12, 1'b0);
  xnor xnor_1 (xnor_1_out, xor_1_out, Input_9);
  xnor xnor_2 (xnor_2_out, xor_2_out, Input_10);
  xnor xnor_3 (xnor_3_out, xor_3_out, Input_11);
  xnor xnor_4 (xnor_4_out, xor_4_out, Input_12);
  not not_1 (not_1_out, xnor_1_out);
  not not_2 (not_2_out, xnor_2_out);
  not not_3 (not_3_out, xnor_1_out);
  not not_4 (not_4_out, xnor_3_out);
  not not_5 (not_5_out, xnor_2_out);
  not not_6 (not_6_out, xnor_3_out);
  not not_7 (not_7_out, xnor_1_out);
  not not_8 (not_8_out, xnor_2_out);
  not not_9 (not_9_out, xnor_3_out);
  not not_10 (not_10_out, xnor_1_out);
  not not_11 (not_11_out, xnor_4_out);
  not not_12 (not_12_out, xnor_2_out);
  not not_13 (not_13_out, xnor_4_out);
  not not_14 (not_14_out, xnor_1_out);
  not not_15 (not_15_out, xnor_2_out);
  not not_16 (not_16_out, xnor_4_out);
  not not_17 (not_17_out, xnor_3_out);
  not not_18 (not_18_out, xnor_4_out);
  and and_1 (and_1_out, not_1_out, not_2_out, xnor_3_out, xnor_4_out);
  and and_2 (and_2_out, not_3_out, xnor_2_out, not_4_out, xnor_4_out);
  and and_3 (and_3_out, xnor_1_out, not_5_out, not_6_out, xnor_4_out);
  and and_4 (and_4_out, not_7_out, not_8_out, not_9_out, xnor_4_out);
  and and_5 (and_5_out, not_10_out, xnor_2_out, xnor_3_out, not_11_out);
  and and_6 (and_6_out, xnor_1_out, not_12_out, xnor_3_out, not_13_out);
  and and_7 (and_7_out, not_14_out, not_15_out, xnor_3_out, not_16_out);
  and and_8 (and_8_out, xnor_1_out, xnor_2_out, not_17_out, not_18_out);
  xor xor_6 (Output_1, Input_1, and_1_out);
  xor xor_7 (Output_2, Input_2, and_2_out);
  xor xor_8 (Output_3, Input_3, and_3_out);
  xor xor_9 (Output_4, Input_4, and_4_out);
  xor xor_10 (Output_5, Input_5, and_5_out);
  xor xor_11 (Output_6, Input_6, and_6_out);
  xor xor_12 (Output_7, Input_7, and_7_out);
  xor xor_13 (Output_8, Input_8, and_8_out);
  xor xor_14 (Output_9, Input_13, xor_5_out);
endmodule

module crc_generator (
  input  Input_1,
  input  Input_2,
  input  Input_3,
  input  Input_4,
  input  Input_5,
  input  Input_6,
  input  Input_7,
  input  Input_8,
  input  Clock,
  output Output_1,
  output Output_2,
  output Output_3,
  output Output_4
);

  wire and_1_out, multiplexer_1_out, not_1_out, not_2_out, not_3_out, register_1_q, xor_1_out;
  wire [3:0] counter_1_q;

  Register #(.width(1)) register_1 (.D(xor_1_out), .en(not_1_out), .clk(Clock), .Q(register_1_q));  // open: clr
  xor xor_1 (xor_1_out, multiplexer_1_out, Output_4);
  not not_1 (not_1_out, and_1_out);
  Register #(.width(1)) register_2 (.D(Output_1), .en(not_1_out), .clk(Clock), .Q(Output_2));  // open: clr
  xor xor_2 (Output_1, Output_4, register_1_q);
  Multiplexer #(.select(4)) multiplexer_1 (
    .in0(Input_1), .in1(Input_2), .in2(Input_3), .in3(Input_4), .in4(Input_5), .in5(Input_6), .in6(Input_7),
    .in7(Input_8), .in8(1'b0), .in9(1'b0), .in10(1'b0), .in11(1'b0), .in12(1'b0), .in13(1'b0), .in14(1'b0),
    .in15(1'b0), .out(multiplexer_1_out), .sel(counter_1_q));
  Register #(.width(1)) register_3 (.D(Output_2), .en(not_1_out), .clk(Clock), .Q(Output_3));  // open: clr
  Register #(.width(1)) register_4 (.D(Output_3), .en(not_1_out), .clk(Clock), .Q(Output_4));  // open: clr
  Counter #(.max('hc), .width(4)) counter_1 (
    .load(and_1_out), .D(4'b1100), .count(1'b1), .Q(counter_1_q), .up(1'b1), .clk(Clock), .clr(1'b0));  // open: carry
  not not_2 (not_2_out, counter_1_q[0]);
  not not_3 (not_3_out, counter_1_q[1]);
  and and_1 (and_1_out, counter_1_q[3], counter_1_q[2], not_3_out, not_2_out);
endmodule

module crc_decoder (
  input  Input_1,
  input  Input_2,
  input  Input_3,
  input  Input_4,
  input  Input_5,
  input  Input_6,
  input  Input_7,
  input  Input_8,
  input  Input_9,
  input  Input_10,
  input  Input_11,
  input  Input_12,
  input  Clock,
  output Output_1,
  output Output_2,
  output Output_3,
  output Output_4
);

  wire and_1_out, multiplexer_1_out, not_1_out, not_2_out, not_3_out, register_1_q, xor_1_out;
  wire [3:0] counter_1_q;

  xor xor_1 (xor_1_out, multiplexer_1_out, Output_4);
  Register #(.width(1)) register_1 (.D(xor_1_out), .en(not_1_out), .clk(Clock), .Q(register_1_q));  // open: clr
  not not_1 (not_1_out, and_1_out);
  Multiplexer #(.select(4)) multiplexer_1 (
    .in0(Input_1), .in1(Input_2), .in2(Input_3), .in3(Input_4), .in4(Input_5), .in5(Input_6), .in6(Input_7),
    .in7(Input_8), .in8(Input_9), .in9(Input_10), .in10(Input_11), .in11(Input_12), .in12(1'b0), .in13(1'b0),
    .in14(1'b0), .in15(1'b0), .out(multiplexer_1_out), .sel(counter_1_q));
  Register #(.width(1)) register_2 (.D(Output_1), .en(not_1_out), .clk(Clock), .Q(Output_2));  // open: clr
  xor xor_2 (Output_1, Output_4, register_1_q);
  Register #(.width(1)) register_3 (.D(Output_2), .en(not_1_out), .clk(Clock), .Q(Output_3));  // open: clr
  Register #(.width(1)) register_4 (.D(Output_3), .en(not_1_out), .clk(Clock), .Q(Output_4));  // open: clr
  Counter #(.max('hc), .width(4)) counter_1 (
    .load(and_1_out), .D(4'b1100), .count(1'b1), .Q(counter_1_q), .up(1'b1), .clk(Clock), .clr(1'b0));  // open: carry
  not not_2 (not_2_out, counter_1_q[1]);
  not not_3 (not_3_out, counter_1_q[0]);
  and and_1 (and_1_out, counter_1_q[3], counter_1_q[2], not_2_out, not_3_out);
endmodule
