// Logisim project Phone_Number_Project.circ as structural Verilog: 11 circuits, main circuit main
module main (
  input  in_1,
  input  in_2
);

  wire a_1_out_2, a_2_out_2, a_3_out_2, b_1_out_2, b_2_out_2, b_3_out_2, c_1_out_2, c_2_out_2, c_3_out_2,
       d_1_out_2, d_2_out_2, d_3_out_2, e_1_out_2, e_2_out_2, e_3_out_2, f_1_out_2, f_2_out_2, f_3_out_2,
       g_1_out_2, g_2_out_2, g_3_out_2;
  wire [2:0] threebitcounter_1_out_2, threebitcounterfivelooper_1_out_1, threebitcounterjk_1_out_2;

  ThreeBitCounter threebitcounter_1 (.in_1(in_1), .out_2(threebitcounter_1_out_2));
  ThreeBitCounterFiveLooper threebitcounterfivelooper_1 (.out_1(threebitcounterfivelooper_1_out_1));
  ThreeBitCounterJK threebitcounterjk_1 (.in_1(in_2), .out_2(threebitcounterjk_1_out_2));
  A a_1 (.Ain(threebitcounter_1_out_2), .out_2(a_1_out_2));
  B b_1 (.Bin(threebitcounter_1_out_2), .out_2(b_1_out_2));
  C c_1 (.Cin(threebitcounter_1_out_2), .out_2(c_1_out_2));
  D d_1 (.Din(threebitcounter_1_out_2), .out_2(d_1_out_2));
  E e_1 (.Ein(threebitcounter_1_out_2), .out_2(e_1_out_2));
  F f_1 (.Fin(threebitcounter_1_out_2), .out_2(f_1_out_2));
  G g_1 (.Gin(threebitcounter_1_out_2), .out_2(g_1_out_2));
  A a_2 (.Ain(threebitcounterfivelooper_1_out_1), .out_2(a_2_out_2));
  B b_2 (.Bin(threebitcounterfivelooper_1_out_1), .out_2(b_2_out_2));
  C c_2 (.Cin(threebitcounterfivelooper_1_out_1), .out_2(c_2_out_2));
  D d_2 (.Din(threebitcounterfivelooper_1_out_1), .out_2(d_2_out_2));
  E e_2 (.Ein(threebitcounterfivelooper_1_out_1), .out_2(e_2_out_2));
  F f_2 (.Fin(threebitcounterfivelooper_1_out_1), .out_2(f_2_out_2));
  G g_2 (.Gin(threebitcounterfivelooper_1_out_1), .out_2(g_2_out_2));
  A a_3 (.Ain(threebitcounterjk_1_out_2), .out_2(a_3_out_2));
  B b_3 (.Bin(threebitcounterjk_1_out_2), .out_2(b_3_out_2));
  C c_3 (.Cin(threebitcounterjk_1_out_2), .out_2(c_3_out_2));
  D d_3 (.Din(threebitcounterjk_1_out_2), .out_2(d_3_out_2));
  E e_3 (.Ein(threebitcounterjk_1_out_2), .out_2(e_3_out_2));
  F f_3 (.Fin(threebitcounterjk_1_out_2), .out_2(f_3_out_2));
  G g_3 (.Gin(threebitcounterjk_1_out_2), .out_2(g_3_out_2));
  _7_Segment_Display u_7_segment_display_1 (
    .g(g_1_out_2), .f(f_1_out_2), .a(a_1_out_2), .b(b_1_out_2), .e(e_1_out_2), .d(d_1_out_2), .c(c_1_out_2));  // open: dp
  _7_Segment_Display u_7_segment_display_2 (
    .g(g_2_out_2), .f(f_2_out_2), .a(a_2_out_2), .b(b_2_out_2), .e(e_2_out_2), .d(d_2_out_2), .c(c_2_out_2));  // open: dp
  _7_Segment_Display u_7_segment_display_3 (
    .g(g_3_out_2), .f(f_3_out_2), .a(a_3_out_2), .b(b_3_out_2), .e(e_3_out_2), .d(d_3_out_2), .c(c_3_out_2));  // open: dp
endmodule

module A (
  input  [2:0] Ain,
  output out_2
);

  wire nor_1_out, nor_2_out, nor_3_out, not_1_out, not_2_out;

  not not_1 (not_1_out, Ain[1]);
  not not_2 (not_2_out, Ain[0]);
  nor nor_1 (nor_1_out, not_1_out, Ain[2]);
  nor nor_2 (nor_2_out, nor_1_out, nor_1_out);
  nor nor_3 (nor_3_out, nor_2_out, not_2_out);
  nor nor_4 (out_2, nor_3_out, nor_3_out);
endmodule

module B (
  input  [2:0] Bin,
  output out_2
);

  nand nand_1 (out_2, Bin[1], Bin[0]);
  // OR_Gate or_1 is placed but not wired
endmodule

module C (
  input  [2:0] Cin,
  output out_2
);

  wire and_1_out, and_2_out, not_1_out, not_2_out, not_3_out, or_1_out;

  not not_1 (not_1_out, Cin[1]);
  not not_2 (not_2_out, Cin[0]);
  and and_1 (and_1_out, not_2_out, not_3_out);
  not not_3 (not_3_out, Cin[2]);
  and and_2 (and_2_out, Cin[2], Cin[0]);
  or or_1 (or_1_out, not_1_out, and_1_out);
  or or_2 (out_2, or_1_out, and_2_out);
endmodule

module D (
  input  [2:0] Din,
  output out_2
);

  wire not_1_out, not_2_out, or_1_out;

  not not_1 (not_1_out, Din[0]);
  not not_2 (not_2_out, Din[1]);
  or or_1 (or_1_out, not_1_out, not_2_out);
  or or_2 (out_2, or_1_out, Din[2]);
endmodule

module E (
  input  [2:0] Ein,
  output out_2
);

  wire and_1_out, and_2_out, and_3_out, not_1_out, not_2_out, not_3_out, or_1_out;

  not not_1 (not_1_out, Ein[0]);
  not not_2 (not_2_out, Ein[1]);
  not not_3 (not_3_out, Ein[2]);
  and and_1 (and_1_out, Ein[1], not_1_out);
  and and_2 (and_2_out, not_1_out, Ein[2]);
  and and_3 (and_3_out, not_3_out, not_2_out, Ein[0]);
  or or_1 (or_1_out, and_1_out, and_2_out);
  or or_2 (out_2, or_1_out, and_3_out);
endmodule

module F (
  input  [2:0] Fin,
  output out_2
);

  wire and_1_out, and_2_out, and_3_out, and_4_out, not_1_out, not_2_out, not_3_out, or_1_out, or_2_out;

  not not_1 (not_1_out, Fin[0]);
  not not_2 (not_2_out, Fin[1]);
  not not_3 (not_3_out, Fin[2]);
  and and_1 (and_1_out, not_1_out, not_2_out, Fin[2]);
  and and_2 (and_2_out, not_1_out, Fin[1], not_3_out);
  and and_3 (and_3_out, Fin[0], not_2_out, not_3_out);
  and and_4 (and_4_out, Fin[2], Fin[0], Fin[1]);
  or or_1 (or_1_out, and_1_out, and_2_out);
  or or_2 (or_2_out, and_3_out, and_4_out);
  or or_3 (out_2, or_1_out, or_2_out);
endmodule

module G (
  input  [2:0] Gin,
  output out_2
);

  wire and_1_out, and_2_out, not_1_out, not_2_out, or_1_out;

  not not_1 (not_1_out, Gin[1]);
  not not_2 (not_2_out, Gin[2]);
  and and_1 (and_1_out, Gin[2], Gin[1]);
  or or_1 (or_1_out, and_1_out, and_2_out);
  and and_2 (and_2_out, not_1_out, not_2_out);
  or or_2 (out_2, or_1_out, Gin[0]);
endmodule

module ThreeBitCounter (
  input  in_1,
  output [2:0] out_2
);

  wire and_1_out, clock_1_out, d_ff_1_q, d_ff_2_q, d_ff_3_q, d_ff_3_qn, xor_1_out, xor_2_out;

  Clock clock_1 (.out(clock_1_out));
  D_Flip_Flop d_ff_1 (.D(xor_1_out), .clk(clock_1_out), .Q(d_ff_1_q));  // open: Qn, preset, reset
  D_Flip_Flop d_ff_2 (.D(xor_2_out), .clk(clock_1_out), .Q(d_ff_2_q));  // open: Qn, preset, reset
  and and_1 (and_1_out, d_ff_3_q, d_ff_2_q);
  D_Flip_Flop d_ff_3 (.D(d_ff_3_qn), .clk(clock_1_out), .Q(d_ff_3_q), .Qn(d_ff_3_qn));  // open: preset, reset
  xor xor_1 (xor_1_out, d_ff_1_q, and_1_out);
  xor xor_2 (xor_2_out, d_ff_2_q, d_ff_3_q);
  xor xor_3 (out_2[0], in_1, d_ff_3_q);
  xor xor_4 (out_2[1], in_1, d_ff_2_q);
  xor xor_5 (out_2[2], in_1, d_ff_1_q);
endmodule

module ThreeBitCounterFiveLooper (
  output [2:0] out_1
);

  wire and_1_out, and_2_out, and_3_out, and_4_out, and_5_out, clock_1_out, d_ff_1_qn, d_ff_2_qn, d_ff_3_qn,
       or_1_out, or_2_out, xor_1_out;

  D_Flip_Flop d_ff_1 (.D(or_1_out), .clk(clock_1_out), .Q(out_1[2]), .Qn(d_ff_1_qn));  // open: preset, reset
  Clock clock_1 (.out(clock_1_out));
  D_Flip_Flop d_ff_2 (.D(and_5_out), .clk(clock_1_out), .Q(out_1[1]), .Qn(d_ff_2_qn));  // open: preset, reset
  and and_1 (and_1_out, d_ff_3_qn, d_ff_2_qn, out_1[2]);
  and and_2 (and_2_out, d_ff_1_qn, out_1[1], out_1[0]);
  D_Flip_Flop d_ff_3 (.D(or_2_out), .clk(clock_1_out), .Q(out_1[0]), .Qn(d_ff_3_qn));  // open: preset, reset
  or or_1 (or_1_out, and_1_out, and_2_out);
  and and_3 (and_3_out, d_ff_1_qn, d_ff_3_qn);
  or or_2 (or_2_out, and_3_out, and_4_out);
  and and_4 (and_4_out, d_ff_2_qn, d_ff_3_qn);
  xor xor_1 (xor_1_out, out_1[1], out_1[0]);
  and and_5 (and_5_out, d_ff_1_qn, xor_1_out);
endmodule

module ThreeBitCounterJK (
  input  in_1,
  output [2:0] out_2
);

  wire and_1_out, clock_1_out, j_k_ff_1_q, j_k_ff_2_q, j_k_ff_3_q;

  Clock clock_1 (.out(clock_1_out));
  J_K_Flip_Flop j_k_ff_1 (.J(and_1_out), .K(and_1_out), .clk(clock_1_out), .Q(j_k_ff_1_q));  // open: Qn, preset, reset
  J_K_Flip_Flop j_k_ff_2 (
    .J(j_k_ff_3_q), .K(j_k_ff_3_q), .clk(clock_1_out), .Q(j_k_ff_2_q));  // open: Qn, preset, reset
  J_K_Flip_Flop j_k_ff_3 (.J(1'b1), .K(1'b1), .clk(clock_1_out), .Q(j_k_ff_3_q));  // open: Qn, preset, reset
  and and_1 (and_1_out, j_k_ff_2_q, j_k_ff_3_q);
  xor xor_1 (out_2[2], in_1, j_k_ff_1_q);
  xor xor_2 (out_2[1], in_1, j_k_ff_2_q);
  xor xor_3 (out_2[0], in_1, j_k_ff_3_q);
endmodule
