// Logisim project Programmable_Counter.circ as structural Verilog: 1 circuit, main circuit main
module main (
  input  in_1,
  input  in_2,
  input  in_3,
  input  in_4,
  input  in_5,
  input  in_6,
  input  in_7,
  input  in_8,
  input  in_9,
  input  in_10,
  input  in_11,
  input  in_12,
  output [3:0] out_13,
  output out_14,
  output [3:0] Count1,
  output Carry1
);

  wire and_1_out, clock_1_out, clock_2_out, xnor_1_out, xnor_2_out, xnor_3_out, xnor_4_out;

  Clock clock_1 (.out(clock_1_out));
  Clock clock_2 (.out(clock_2_out));
  Counter #(.max('hf), .width(4)) counter_1 (
    .load(out_14), .D({in_1, in_2, in_3, in_4}), .count(1'b1), .Q(out_13), .carry(out_14), .up(1'b1),
    .clk(clock_1_out), .clr(1'b0));
  Counter #(.max('hf), .width(4)) counter_2 (
    .load(and_1_out), .D({in_9, in_10, in_11, in_12}), .count(1'b1), .Q(Count1), .carry(Carry1), .up(1'b1),
    .clk(clock_2_out), .clr(1'b0));
  xnor xnor_1 (xnor_1_out, in_5, Count1[3]);
  xnor xnor_2 (xnor_2_out, in_6, Count1[2]);
  xnor xnor_3 (xnor_3_out, Count1[1], in_7);
  and and_1 (and_1_out, xnor_1_out, xnor_2_out, xnor_3_out, xnor_4_out);
  xnor xnor_4 (xnor_4_out, Count1[0], in_8);
  // Digital_Oscilloscope digital_oscilloscope_1: pin names not known; wires that end beside it: clock_1_out, out_13[3], out_13[2], out_13[1], out_13[0], out_14
  // Digital_Oscilloscope digital_oscilloscope_2: pin names not known; wires that end beside it: clock_2_out, Count1[3], Count1[2], Count1[1], Count1[0], and_1_out
endmodule
