// Logisim project Security_System_Controller.circ as structural Verilog: 22 circuits, main circuit main
module main (
  output LSB,
  output out_2,
  output out_3,
  output MSB
);

  wire button_1_out, button_2_out, button_3_out, button_4_out, button_5_out, clock_1_out,
       level_1_proximity_detector_1_led_1, level_2_structure_detector_1_led_2,
       level_2_structure_detector_1_led_3, PD_SD_sw1, PD_SD_sw2;
  wire [1:0] two_bit_counter_1_count1;
  wire [6:0] level_1_proximity_detector_1_out_4, level_2_structure_detector_1_ssd_2,
       level_2_structure_detector_1_ssd_3, multiplexer_1_out;

  Clock clock_1 (.out(clock_1_out));
  DipSwitch #(.number(2)) PD_SD (.sw1(PD_SD_sw1), .sw2(PD_SD_sw2));
  Button button_1 (.out(button_1_out));
  Button button_2 (.out(button_2_out));
  Button button_3 (.out(button_3_out));
  Button button_4 (.out(button_4_out));
  Button button_5 (.out(button_5_out));
  LED LED_1 (.in(level_1_proximity_detector_1_led_1));
  Level_1_Proximity_Detector level_1_proximity_detector_1 (
    .PD(PD_SD_sw1), .Clock(clock_1_out), .LED_1(level_1_proximity_detector_1_led_1),
    .out_4(level_1_proximity_detector_1_out_4));
  LED LED_2 (.in(level_2_structure_detector_1_led_2));
  Level_2_Structure_Detector level_2_structure_detector_1 (
    .SD(PD_SD_sw2), .Clock(clock_1_out), .in_3(button_1_out), .in_4(button_2_out), .in_5(button_3_out),
    .in_6(button_4_out), .in_7(button_5_out), .LED_2(level_2_structure_detector_1_led_2),
    .LED_3(level_2_structure_detector_1_led_3), .SSD_2(level_2_structure_detector_1_ssd_2),
    .SSD_3(level_2_structure_detector_1_ssd_3));
  _7_Segment_Display #(.active("false")) u_7_segment_display_1 (
    .g(level_1_proximity_detector_1_out_4[6]), .f(level_1_proximity_detector_1_out_4[5]),
    .a(level_1_proximity_detector_1_out_4[0]), .b(level_1_proximity_detector_1_out_4[1]),
    .e(level_1_proximity_detector_1_out_4[4]), .d(level_1_proximity_detector_1_out_4[3]),
    .c(level_1_proximity_detector_1_out_4[2]));  // open: dp
  LED LED_3 (.in(level_2_structure_detector_1_led_3));
  _7_Segment_Display #(.active("false")) u_7_segment_display_2 (
    .g(1'b1), .f(1'b0), .a(1'b0), .b(1'b0), .e(1'b0), .d(1'b0), .c(1'b0));  // open: dp
  Multiplexer #(.select(2), .width(7)) multiplexer_1 (
    .in0(level_1_proximity_detector_1_out_4), .in1(7'b1000000), .in2(level_2_structure_detector_1_ssd_2),
    .in3(level_2_structure_detector_1_ssd_3), .out(multiplexer_1_out), .sel(two_bit_counter_1_count1));
  two_bit_counter two_bit_counter_1 (.Clock(clock_1_out), .Count1(two_bit_counter_1_count1));
  _7_Segment_Display #(.active("false")) u_7_segment_display_3 (
    .g(level_2_structure_detector_1_ssd_2[6]), .f(level_2_structure_detector_1_ssd_2[5]),
    .a(level_2_structure_detector_1_ssd_2[0]), .b(level_2_structure_detector_1_ssd_2[1]),
    .e(level_2_structure_detector_1_ssd_2[4]), .d(level_2_structure_detector_1_ssd_2[3]),
    .c(level_2_structure_detector_1_ssd_2[2]));  // open: dp
  _7_Segment_Display #(.active("false")) u_7_segment_display_4 (
    .g(level_2_structure_detector_1_ssd_3[6]), .f(level_2_structure_detector_1_ssd_3[5]),
    .a(level_2_structure_detector_1_ssd_3[0]), .b(level_2_structure_detector_1_ssd_3[1]),
    .e(level_2_structure_detector_1_ssd_3[4]), .d(level_2_structure_detector_1_ssd_3[3]),
    .c(level_2_structure_detector_1_ssd_3[2]));  // open: dp
  Demultiplexer #(.enable("true"), .select(2)) demultiplexer_1 (
    .out0(LSB), .out1(out_2), .out2(out_3), .out3(MSB), .in(1'b1), .sel(two_bit_counter_1_count1), .en(1'b1));
  _7_Segment_Display #(.active("false")) u_7_segment_display_5 (
    .g(multiplexer_1_out[6]), .f(multiplexer_1_out[5]), .a(multiplexer_1_out[0]), .b(multiplexer_1_out[1]),
    .e(multiplexer_1_out[4]), .d(multiplexer_1_out[3]), .c(multiplexer_1_out[2]));  // open: dp
endmodule

module edge_detector (
  input  Input_Val,
  input  Clock,
  output out_3
);

  wire and_1_out, and_2_out, and_3_out, d_ff_1_q, d_ff_1_qn, d_ff_2_q, d_ff_2_qn, or_1_out, or_2_out;

  and and_1 (and_1_out, Input_Val, d_ff_2_q, d_ff_1_qn);
  and and_2 (and_2_out, Input_Val, d_ff_2_q, d_ff_1_q);
  and and_3 (and_3_out, d_ff_1_qn, Input_Val, d_ff_2_qn);
  or or_1 (or_1_out, and_1_out, out_3, and_2_out);
  or or_2 (or_2_out, and_2_out, out_3, and_3_out);
  D_Flip_Flop d_ff_1 (.D(or_1_out), .clk(Clock), .Q(d_ff_1_q), .Qn(d_ff_1_qn));  // open: preset, reset
  D_Flip_Flop d_ff_2 (.D(or_2_out), .clk(Clock), .Q(d_ff_2_q), .Qn(d_ff_2_qn));  // open: preset, reset
  and and_4 (out_3, d_ff_1_q, d_ff_2_qn);
endmodule

module Qc_Next_State (
  input  Qa,
  input  Qb,
  input  Qc,
  input  E1,
  input  E2,
  input  E3,
  input  E4,
  input  E5,
  input  Lock,
  input  Disengage,
  output out_11
);

  wire and_1_out, and_2_out, and_3_out, and_4_out, and_5_out, and_6_out, and_7_out, and_8_out, and_9_out,
       and_10_out, and_11_out, and_12_out, not_1_out, not_2_out, not_3_out, not_4_out, not_5_out, not_6_out,
       not_7_out, not_8_out, not_9_out;

  not not_1 (not_1_out, Qa);
  not not_2 (not_2_out, Qb);
  not not_3 (not_3_out, Qc);
  not not_4 (not_4_out, E1);
  not not_5 (not_5_out, E2);
  not not_6 (not_6_out, E3);
  not not_7 (not_7_out, E4);
  not not_8 (not_8_out, E5);
  not not_9 (not_9_out, Lock);
  and and_1 (and_1_out, not_1_out, not_2_out, not_3_out, not_4_out, E2, not_6_out, not_7_out, not_8_out, not_9_out);
  and and_2 (and_2_out, not_1_out, not_2_out, Qc, not_4_out, not_5_out, not_6_out, not_7_out, not_8_out, not_9_out);
  and and_3 (and_3_out, not_1_out, Qb, not_3_out, not_4_out, not_5_out, E3, not_7_out, not_8_out, not_9_out);
  and and_4 (and_4_out, not_1_out, Qb, Qc, not_4_out, not_5_out, not_6_out, not_7_out, not_8_out, not_9_out);
  and and_5 (and_5_out, Qa, not_2_out, not_3_out, not_4_out, not_5_out, not_6_out, E4, not_8_out, not_9_out);
  and and_6 (and_6_out, Qa, not_2_out, Qc, not_4_out, not_9_out);
  and and_7 (and_7_out, and_1_out, Disengage);
  and and_8 (and_8_out, and_2_out, Disengage);
  and and_9 (and_9_out, and_3_out, Disengage);
  and and_10 (and_10_out, and_4_out, Disengage);
  and and_11 (and_11_out, and_5_out, Disengage);
  and and_12 (and_12_out, and_6_out, Disengage);
  or or_1 (out_11, and_7_out, and_8_out, and_9_out, and_10_out, and_11_out, and_12_out);
endmodule

module Qb_Next_State (
  input  Qa,
  input  Qb,
  input  Qc,
  input  E1,
  input  E2,
  input  E3,
  input  E4,
  input  E5,
  input  Lock,
  input  Disengage,
  output out_11
);

  wire and_1_out, and_2_out, and_3_out, and_4_out, and_5_out, and_6_out, and_7_out, and_8_out, not_1_out,
       not_2_out, not_3_out, not_4_out, not_5_out, not_6_out, not_7_out, not_8_out, not_9_out;

  not not_1 (not_1_out, Qa);
  not not_2 (not_2_out, Qb);
  not not_3 (not_3_out, Qc);
  not not_4 (not_4_out, E1);
  not not_5 (not_5_out, E2);
  not not_6 (not_6_out, E3);
  not not_7 (not_7_out, E4);
  not not_8 (not_8_out, E5);
  not not_9 (not_9_out, Lock);
  and and_1 (and_1_out, not_1_out, not_2_out, Qc, not_4_out, not_5_out, not_6_out, not_7_out, E5, not_9_out);
  and and_2 (and_2_out, not_1_out, Qb, not_3_out, not_4_out, not_5_out, not_6_out, not_7_out, not_8_out, not_9_out);
  and and_3 (and_3_out, not_1_out, Qb, not_3_out, not_4_out, not_5_out, E3, not_7_out, not_8_out, not_9_out);
  and and_4 (and_4_out, not_1_out, Qb, Qb, not_4_out, not_5_out, not_6_out, not_7_out, not_8_out, not_9_out);
  and and_5 (and_5_out, and_1_out, Disengage);
  and and_6 (and_6_out, and_2_out, Disengage);
  and and_7 (and_7_out, and_3_out, Disengage);
  and and_8 (and_8_out, and_4_out, Disengage);
  or or_1 (out_11, and_5_out, and_6_out, and_7_out, and_8_out);
endmodule

module Qa_Next_State (
  input  Qa,
  input  Qb,
  input  Qc,
  input  E1,
  input  E2,
  input  E3,
  input  E4,
  input  E5,
  input  Lock,
  input  Disengage,
  output out_11
);

  wire and_1_out, and_2_out, and_3_out, and_4_out, and_5_out, and_6_out, and_7_out, and_8_out, not_1_out,
       not_2_out, not_3_out, not_4_out, not_5_out, not_6_out, not_7_out, not_8_out, not_9_out;

  not not_1 (not_1_out, Qa);
  not not_2 (not_2_out, Qb);
  not not_3 (not_3_out, Qc);
  not not_4 (not_4_out, E1);
  not not_5 (not_5_out, E2);
  not not_6 (not_6_out, E3);
  not not_7 (not_7_out, E4);
  not not_8 (not_8_out, E5);
  not not_9 (not_9_out, Lock);
  and and_1 (and_1_out, not_1_out, Qb, Qc, E1, not_5_out, not_6_out, not_7_out, not_8_out, not_9_out);
  and and_2 (and_2_out, Qa, not_2_out, not_3_out, not_4_out, not_5_out, not_6_out, not_7_out, not_8_out, not_9_out);
  and and_3 (and_3_out, Qa, not_2_out, not_3_out, not_4_out, not_5_out, not_6_out, E4, not_8_out, not_9_out);
  and and_4 (and_4_out, Qa, not_2_out, Qc, not_4_out, not_9_out);
  and and_5 (and_5_out, and_1_out, Disengage);
  and and_6 (and_6_out, and_2_out, Disengage);
  and and_7 (and_7_out, Disengage, and_3_out);
  and and_8 (and_8_out, Disengage, and_4_out);
  or or_1 (out_11, and_5_out, and_6_out, and_7_out, and_8_out);
endmodule

module keypad (
  input  Clock,
  input  E1,
  input  E2,
  input  E3,
  input  E4,
  input  E5,
  input  Lock,
  output Engage,
  output Value,
  output Disengage
);

  wire d_ff_1_q, d_ff_2_q, d_ff_2_qn, d_ff_3_q, d_ff_4_q, d_ff_5_q, d_ff_5_qn, d_ff_6_q,
       edge_detector_1_out_3, edge_detector_2_out_3, edge_detector_3_out_3, edge_detector_4_out_3,
       edge_detector_5_out_3, edge_detector_6_out_3, edge_detector_7_out_3, edge_detector_8_out_3,
       edge_detector_9_out_3, edge_detector_10_out_3, not_1_out, qa_next_state_1_out_11,
       qa_next_state_2_out_11, qb_next_state_1_out_11, qb_next_state_2_out_11, qc_next_state_1_out_11,
       qc_next_state_2_out_11;

  not not_1 (not_1_out, 1'b0);
  edge_detector edge_detector_1 (.Input_Val(E1), .Clock(Clock), .out_3(edge_detector_1_out_3));
  edge_detector edge_detector_2 (.Input_Val(E2), .Clock(Clock), .out_3(edge_detector_2_out_3));
  edge_detector edge_detector_3 (.Input_Val(E3), .Clock(Clock), .out_3(edge_detector_3_out_3));
  edge_detector edge_detector_4 (.Input_Val(E4), .Clock(Clock), .out_3(edge_detector_4_out_3));
  edge_detector edge_detector_5 (.Input_Val(E5), .Clock(Clock), .out_3(edge_detector_5_out_3));
  edge_detector edge_detector_6 (.Input_Val(E1), .Clock(Clock), .out_3(edge_detector_6_out_3));
  edge_detector edge_detector_7 (.Input_Val(E2), .Clock(Clock), .out_3(edge_detector_7_out_3));
  edge_detector edge_detector_8 (.Input_Val(E3), .Clock(Clock), .out_3(edge_detector_8_out_3));
  edge_detector edge_detector_9 (.Input_Val(E4), .Clock(Clock), .out_3(edge_detector_9_out_3));
  edge_detector edge_detector_10 (.Input_Val(E5), .Clock(Clock), .out_3(edge_detector_10_out_3));
  Qa_Next_State qa_next_state_1 (
    .Qa(d_ff_1_q), .Qb(d_ff_2_q), .Qc(d_ff_3_q), .E1(edge_detector_1_out_3), .E2(edge_detector_2_out_3),
    .E3(edge_detector_3_out_3), .E4(edge_detector_4_out_3), .E5(edge_detector_5_out_3), .Lock(Lock),
    .Disengage(not_1_out), .out_11(qa_next_state_1_out_11));
  Qb_Next_State qb_next_state_1 (
    .Qa(d_ff_1_q), .Qb(d_ff_2_q), .Qc(d_ff_3_q), .E1(edge_detector_1_out_3), .E2(edge_detector_2_out_3),
    .E3(edge_detector_3_out_3), .E4(edge_detector_4_out_3), .E5(edge_detector_5_out_3), .Lock(Lock),
    .Disengage(not_1_out), .out_11(qb_next_state_1_out_11));
  Qc_Next_State qc_next_state_1 (
    .Qa(d_ff_1_q), .Qb(d_ff_2_q), .Qc(d_ff_3_q), .E1(edge_detector_1_out_3), .E2(edge_detector_2_out_3),
    .E3(edge_detector_3_out_3), .E4(edge_detector_4_out_3), .E5(edge_detector_5_out_3), .Lock(Lock),
    .Disengage(not_1_out), .out_11(qc_next_state_1_out_11));
  D_Flip_Flop d_ff_1 (.D(qa_next_state_1_out_11), .clk(Clock), .Q(d_ff_1_q));  // open: Qn, preset, reset
  D_Flip_Flop d_ff_2 (.D(qb_next_state_1_out_11), .clk(Clock), .Q(d_ff_2_q), .Qn(d_ff_2_qn));  // open: preset, reset
  D_Flip_Flop d_ff_3 (.D(qc_next_state_1_out_11), .clk(Clock), .Q(d_ff_3_q));  // open: Qn, preset, reset
  D_Flip_Flop d_ff_4 (.D(qa_next_state_2_out_11), .clk(Clock), .Q(d_ff_4_q));  // open: Qn, preset, reset
  Qa_Next_State qa_next_state_2 (
    .Qa(d_ff_4_q), .Qb(d_ff_5_q), .Qc(d_ff_6_q), .E1(edge_detector_6_out_3), .E2(edge_detector_7_out_3),
    .E3(edge_detector_8_out_3), .E4(edge_detector_9_out_3), .E5(edge_detector_10_out_3), .Lock(Lock),
    .Disengage(Engage), .out_11(qa_next_state_2_out_11));
  D_Flip_Flop d_ff_5 (.D(qb_next_state_2_out_11), .clk(Clock), .Q(d_ff_5_q), .Qn(d_ff_5_qn));  // open: preset, reset
  Qb_Next_State qb_next_state_2 (
    .Qa(d_ff_4_q), .Qb(d_ff_5_q), .Qc(d_ff_6_q), .E1(edge_detector_6_out_3), .E2(edge_detector_7_out_3),
    .E3(edge_detector_8_out_3), .E4(edge_detector_9_out_3), .E5(edge_detector_10_out_3), .Lock(Lock),
    .Disengage(Engage), .out_11(qb_next_state_2_out_11));
  D_Flip_Flop d_ff_6 (.D(qc_next_state_2_out_11), .clk(Clock), .Q(d_ff_6_q));  // open: Qn, preset, reset
  Qc_Next_State qc_next_state_2 (
    .Qa(d_ff_4_q), .Qb(d_ff_5_q), .Qc(d_ff_6_q), .E1(edge_detector_6_out_3), .E2(edge_detector_7_out_3),
    .E3(edge_detector_8_out_3), .E4(edge_detector_9_out_3), .E5(edge_detector_10_out_3), .Lock(Lock),
    .Disengage(Engage), .out_11(qc_next_state_2_out_11));
  and and_1 (Engage, d_ff_1_q, d_ff_2_qn, d_ff_3_q);
  and and_2 (Disengage, d_ff_4_q, d_ff_5_qn, d_ff_6_q);
  xor xor_1 (Value, Engage, Disengage);
endmodule

module timer (
  input  TimerActive,
  input  Clock,
  input  Clear,
  output [6:0] Count,
  output Timer_Carry
);

  wire and_1_out, and_2_out, and_3_out, clock_divider_1_divided_clock, not_1_out, not_2_out, not_3_out,
       not_4_out;
  wire [2:0] counter_1_q;

  and and_1 (and_1_out, and_3_out, Clear);
  not not_1 (not_1_out, Clear);
  clock_divider clock_divider_1 (.Clock(Clock), .Divided_Clock(clock_divider_1_divided_clock));
  Counter #(.max('h7), .ongoal("stay"), .width(3)) counter_1 (
    .load(and_2_out), .D(3'b101), .count(and_1_out), .Q(counter_1_q), .up(1'b0), .clk(Clock), .clr(not_1_out));  // open: carry
  and and_2 (and_2_out, and_1_out, Timer_Carry);
  and and_3 (and_3_out, TimerActive, clock_divider_1_divided_clock);
  not not_2 (not_2_out, counter_1_q[2]);
  not not_3 (not_3_out, counter_1_q[1]);
  not not_4 (not_4_out, counter_1_q[0]);
  and and_4 (Timer_Carry, not_2_out, not_3_out, not_4_out);
  Multiplexer #(.select(3), .width(7)) multiplexer_1 (
    .in0({7{1'b0}}), .in1(7'b0000001), .in2(7'b0000010), .in3(7'b0000100), .in4(7'b0001000),
    .in5(7'b0010000), .in6({7{1'b0}}), .in7({7{1'b0}}), .out(Count), .sel(counter_1_q));
endmodule

module clock_divider (
  input  Clock,
  output Divided_Clock
);

  Counter #(.max('h1ff), .width(9)) counter_1 (
    .load(Divided_Clock), .D(9'h12f), .count(1'b1), .carry(Divided_Clock), .up(1'b1), .clk(Clock), .clr(1'b0));  // open: Q
endmodule

module blinker_divider (
  input  Clock,
  output Divided_Clock
);

  Counter #(.max('h1f), .width(5)) counter_1 (
    .load(Divided_Clock), .D({5{1'b0}}), .count(1'b1), .carry(Divided_Clock), .up(1'b1), .clk(Clock),
    .clr(1'b0));  // open: Q
endmodule

module Level_1_Proximity_Detector (
  input  PD,
  input  Clock,
  output LED_1,
  output [6:0] out_4
);

  wire and_1_out, and_2_out, and_3_out, and_4_out, and_5_out, and_6_out, blinker_divider_1_divided_clock,
       d_ff_1_q, d_ff_1_qn, d_ff_2_q, d_ff_2_qn, d_ff_3_q, d_ff_3_qn, j_k_ff_1_q, l1_pd_qa_1_out_7,
       l1_pd_qb_1_out_7, l1_pd_qc_1_out_7, not_1_out, or_1_out, timer_1_timer_carry;

  D_Flip_Flop d_ff_1 (.D(l1_pd_qa_1_out_7), .clk(Clock), .Q(d_ff_1_q), .Qn(d_ff_1_qn));  // open: preset, reset
  D_Flip_Flop d_ff_2 (.D(l1_pd_qb_1_out_7), .clk(Clock), .Q(d_ff_2_q), .Qn(d_ff_2_qn));  // open: preset, reset
  D_Flip_Flop d_ff_3 (.D(l1_pd_qc_1_out_7), .clk(Clock), .Q(d_ff_3_q), .Qn(d_ff_3_qn));  // open: preset, reset
  timer timer_1 (
    .TimerActive(or_1_out), .Clock(Clock), .Clear(or_1_out), .Count(out_4), .Timer_Carry(timer_1_timer_carry));
  not not_1 (not_1_out, timer_1_timer_carry);
  and and_1 (and_1_out, d_ff_1_q, d_ff_2_qn, d_ff_3_q);
  and and_2 (and_2_out, d_ff_1_q, d_ff_2_qn, d_ff_3_qn);
  and and_3 (and_3_out, d_ff_1_qn, d_ff_2_q, d_ff_3_q, not_1_out);
  and and_4 (and_4_out, d_ff_1_qn, d_ff_2_q, d_ff_3_qn, not_1_out);
  and and_5 (and_5_out, d_ff_1_qn, d_ff_2_qn, d_ff_3_q, not_1_out);
  and and_6 (and_6_out, d_ff_1_qn, d_ff_2_qn, d_ff_3_qn, PD);
  L1_PD_Qa l1_pd_qa_1 (
    .Qa(d_ff_1_q), .Qb(d_ff_2_q), .Qc(d_ff_3_q), .Timer_Carry(timer_1_timer_carry), .Lock(1'b0), .PD(PD),
    .out_7(l1_pd_qa_1_out_7));
  L1_PD_Qb l1_pd_qb_1 (
    .Qa(d_ff_1_q), .Qb(d_ff_2_q), .Qc(d_ff_3_q), .Timer_Carry(timer_1_timer_carry), .Lock(1'b0), .PD(PD),
    .out_7(l1_pd_qb_1_out_7));
  L1_PD_Qc l1_pd_qc_1 (
    .Qa(d_ff_1_q), .Qb(d_ff_2_q), .Qc(d_ff_3_q), .Timer_Carry(timer_1_timer_carry), .Lock(1'b0), .PD(PD),
    .out_7(l1_pd_qc_1_out_7));
  blinker_divider blinker_divider_1 (.Clock(Clock), .Divided_Clock(blinker_divider_1_divided_clock));
  or or_1 (or_1_out, and_2_out, and_3_out, and_6_out, and_4_out, and_5_out);
  J_K_Flip_Flop j_k_ff_1 (
    .J(blinker_divider_1_divided_clock), .K(blinker_divider_1_divided_clock), .clk(Clock), .Q(j_k_ff_1_q));  // open: Qn, preset, reset
  Multiplexer multiplexer_1 (.in0(and_1_out), .in1(j_k_ff_1_q), .out(LED_1), .sel(or_1_out));
endmodule

module L1_PD_Qc (
  input  Qa,
  input  Qb,
  input  Qc,
  input  Timer_Carry,
  input  Lock,
  input  PD,
  output out_7
);

  wire and_1_out, and_2_out, and_3_out, and_4_out, not_1_out, not_2_out, not_3_out, not_4_out, not_5_out;

  not not_1 (not_1_out, Qa);
  not not_2 (not_2_out, Qb);
  not not_3 (not_3_out, Qc);
  not not_4 (not_4_out, Timer_Carry);
  not not_5 (not_5_out, Lock);
  // NOT_Gate not_6 has open pins: in=PD, out=open
  and and_1 (and_1_out, not_1_out, not_2_out, not_3_out, not_4_out, not_5_out, PD);
  and and_2 (and_2_out, not_1_out, Qb, not_3_out, not_4_out, not_5_out, PD);
  and and_3 (and_3_out, Qa, not_2_out, not_3_out, Timer_Carry, not_5_out, PD);
  and and_4 (and_4_out, Qa, not_2_out, Qc, PD, not_5_out);
  or or_1 (out_7, and_1_out, and_2_out, and_3_out, and_4_out);
endmodule

module L1_PD_Qb (
  input  Qa,
  input  Qb,
  input  Qc,
  input  Timer_Carry,
  input  Lock,
  input  PD,
  output out_7
);

  wire and_1_out, and_2_out, not_1_out, not_2_out, not_3_out, not_4_out, not_5_out;

  not not_1 (not_1_out, Qa);
  not not_2 (not_2_out, Qb);
  not not_3 (not_3_out, Qc);
  not not_4 (not_4_out, Timer_Carry);
  not not_5 (not_5_out, Lock);
  and and_1 (and_1_out, not_1_out, not_2_out, Qc, not_4_out, not_5_out, PD);
  and and_2 (and_2_out, not_1_out, Qb, not_3_out, not_5_out, not_4_out, PD);
  or or_1 (out_7, and_1_out, and_2_out);
endmodule

module L1_PD_Qa (
  input  Qa,
  input  Qb,
  input  Qc,
  input  Timer_Carry,
  input  Lock,
  input  PD,
  output out_7
);

  wire and_1_out, and_2_out, and_3_out, not_1_out, not_2_out, not_3_out, not_4_out, not_5_out;

  not not_1 (not_1_out, Qa);
  not not_2 (not_2_out, Qb);
  not not_3 (not_3_out, Qc);
  not not_4 (not_4_out, Timer_Carry);
  not not_5 (not_5_out, Lock);
  and and_1 (and_1_out, not_1_out, Qb, Qc, not_4_out, not_5_out, PD);
  and and_2 (and_2_out, Qa, not_2_out, not_3_out, not_5_out, PD);
  and and_3 (and_3_out, Qa, not_2_out, Qc, not_5_out, PD);
  or or_1 (out_7, and_1_out, and_2_out, and_3_out);
endmodule

module Level_2_Structure_Detector (
  input  SD,
  input  Clock,
  input  in_3,
  input  in_4,
  input  in_5,
  input  in_6,
  input  in_7,
  output LED_2,
  output LED_3,
  output [6:0] SSD_2,
  output [6:0] SSD_3
);

  wire and_1_out, and_2_out, blinker_divider_1_divided_clock, d_ff_1_q, d_ff_1_qn, d_ff_2_q, d_ff_2_qn,
       d_ff_3_q, d_ff_3_qn, j_k_ff_1_q, keypad_1_value, l2_led2_1_out_8, l2_sd_qa_1_out_8, l2_sd_qb_1_out_8,
       l2_sd_qc_1_out_8, l2_ta2_1_out_8, not_1_out, not_2_out, or_1_out, timer_1_timer_carry,
       timer_2_timer_carry;

  D_Flip_Flop d_ff_1 (.D(l2_sd_qa_1_out_8), .clk(Clock), .Q(d_ff_1_q), .Qn(d_ff_1_qn));  // open: preset, reset
  D_Flip_Flop d_ff_2 (.D(l2_sd_qb_1_out_8), .clk(Clock), .Q(d_ff_2_q), .Qn(d_ff_2_qn));  // open: preset, reset
  D_Flip_Flop d_ff_3 (.D(l2_sd_qc_1_out_8), .clk(Clock), .Q(d_ff_3_q), .Qn(d_ff_3_qn));  // open: preset, reset
  keypad keypad_1 (
    .Clock(Clock), .E1(in_3), .E2(in_4), .E3(in_5), .E4(in_6), .E5(in_7), .Lock(1'b1), .Value(keypad_1_value));  // open: Engage, Disengage
  and and_1 (and_1_out, d_ff_3_qn, d_ff_2_qn, d_ff_1_q);
  not not_1 (not_1_out, and_1_out);
  and and_2 (and_2_out, d_ff_1_qn, d_ff_2_qn, d_ff_3_q);
  not not_2 (not_2_out, and_2_out);
  or or_1 (or_1_out, not_2_out, not_1_out);
  L2_SD_Qa l2_sd_qa_1 (
    .Qa(d_ff_1_q), .Qb(d_ff_2_q), .Qc(d_ff_3_q), .KP(keypad_1_value), .SD(SD), .TC2(timer_1_timer_carry),
    .TC3(timer_2_timer_carry), .out_8(l2_sd_qa_1_out_8));
  L2_SD_Qb l2_sd_qb_1 (
    .Qa(d_ff_1_q), .Qb(d_ff_2_q), .Qc(d_ff_3_q), .KP(keypad_1_value), .SD(SD), .TC2(timer_1_timer_carry),
    .TC3(timer_2_timer_carry), .out_8(l2_sd_qb_1_out_8));
  L2_SD_Qc l2_sd_qc_1 (
    .Qa(d_ff_1_q), .Qb(d_ff_2_q), .Qc(d_ff_3_q), .KP(keypad_1_value), .SD(SD), .TC2(timer_1_timer_carry),
    .TC3(timer_2_timer_carry), .out_8(l2_sd_qc_1_out_8));
  L2_LED2 l2_led2_1 (
    .Qa(d_ff_1_q), .Qb(d_ff_2_q), .Qc(d_ff_3_q), .KP(keypad_1_value), .SD(SD), .TC2(timer_1_timer_carry),
    .TC3(timer_2_timer_carry), .out_8(l2_led2_1_out_8));
  L2_LED3 l2_led3_1 (.Qa(d_ff_1_q), .Qb(d_ff_2_q), .Qc(d_ff_3_q), .KP(keypad_1_value), .out_5(LED_3));
  L2_TA2 l2_ta2_1 (
    .Qa(d_ff_1_q), .Qb(d_ff_2_q), .Qc(d_ff_3_q), .KP(keypad_1_value), .SD(SD), .TC2(timer_1_timer_carry),
    .TC3(timer_2_timer_carry), .out_8(l2_ta2_1_out_8));
  L2_TA3 l2_ta3_1 (
    .Qa(d_ff_1_q), .Qb(d_ff_2_q), .Qc(d_ff_3_q), .KP(keypad_1_value), .SD(SD), .TC2(timer_1_timer_carry),
    .TC3(timer_2_timer_carry), .out_8(l2_led2_1_out_8));
  timer timer_1 (
    .TimerActive(l2_ta2_1_out_8), .Clock(Clock), .Clear(not_1_out), .Count(SSD_2),
    .Timer_Carry(timer_1_timer_carry));
  timer timer_2 (
    .TimerActive(l2_led2_1_out_8), .Clock(Clock), .Clear(or_1_out), .Count(SSD_3),
    .Timer_Carry(timer_2_timer_carry));
  blinker_divider blinker_divider_1 (.Clock(Clock), .Divided_Clock(blinker_divider_1_divided_clock));
  J_K_Flip_Flop j_k_ff_1 (
    .J(blinker_divider_1_divided_clock), .K(blinker_divider_1_divided_clock), .clk(Clock), .Q(j_k_ff_1_q));  // open: Qn, preset, reset
  Multiplexer multiplexer_1 (.in0(1'b0), .in1(j_k_ff_1_q), .out(LED_2), .sel(l2_led2_1_out_8));
endmodule

module L2_SD_Qc (
  input  Qa,
  input  Qb,
  input  Qc,
  input  KP,
  input  SD,
  input  TC2,
  input  TC3,
  output out_8
);

  wire and_1_out, and_2_out, and_3_out, and_4_out, and_5_out, and_6_out, and_7_out, not_1_out, not_2_out,
       not_3_out, not_4_out, not_5_out;

  not not_1 (not_1_out, Qa);
  not not_2 (not_2_out, Qb);
  not not_3 (not_3_out, Qc);
  not not_4 (not_4_out, SD);
  not not_5 (not_5_out, TC2);
  // NOT_Gate not_6 has open pins: in=TC3, out=open
  and and_1 (and_1_out, not_1_out, not_2_out, not_3_out, KP, SD);
  and and_2 (and_2_out, not_1_out, not_2_out, Qc, KP, not_4_out, not_5_out);
  and and_3 (and_3_out, not_1_out, Qb, not_3_out, KP, SD);
  and and_4 (and_4_out, not_1_out, Qb, Qc, KP, not_4_out);
  and and_5 (and_5_out, Qa, not_2_out, not_3_out, KP, not_4_out);
  and and_6 (and_6_out, Qa, not_2_out, not_3_out, KP, SD, TC2, TC3);
  and and_7 (and_7_out, Qa, not_2_out, Qc, KP);
  or or_1 (out_8, and_1_out, and_2_out, and_3_out, and_4_out, and_5_out, and_6_out, and_7_out);
endmodule

module L2_SD_Qb (
  input  Qa,
  input  Qb,
  input  Qc,
  input  KP,
  input  SD,
  input  TC2,
  input  TC3,
  output out_8
);

  wire and_1_out, and_2_out, and_3_out, and_4_out, and_5_out, not_1_out, not_2_out, not_3_out, not_4_out;

  not not_1 (not_1_out, Qa);
  not not_2 (not_2_out, Qb);
  not not_3 (not_3_out, Qc);
  not not_4 (not_4_out, SD);
  // NOT_Gate not_5 has open pins: in=TC2, out=open
  // NOT_Gate not_6 has open pins: in=TC3, out=open
  and and_1 (and_1_out, not_1_out, not_2_out, Qc, KP, SD, TC2);
  and and_2 (and_2_out, not_1_out, Qb, not_3_out, KP, not_4_out);
  and and_3 (and_3_out, not_1_out, Qb, not_3_out, KP, SD);
  and and_4 (and_4_out, not_1_out, Qb, Qc, KP, not_4_out);
  and and_5 (and_5_out, Qa, not_2_out, not_3_out, KP, not_4_out);
  or or_1 (out_8, and_1_out, and_2_out, and_3_out, and_4_out, and_5_out);
endmodule

module L2_SD_Qa (
  input  Qa,
  input  Qb,
  input  Qc,
  input  KP,
  input  SD,
  input  TC2,
  input  TC3,
  output out_8
);

  wire and_1_out, and_2_out, and_3_out, and_4_out, not_1_out, not_2_out, not_3_out, not_5_out, not_6_out;

  not not_1 (not_1_out, Qa);
  not not_2 (not_2_out, Qb);
  not not_3 (not_3_out, Qc);
  // NOT_Gate not_4 has open pins: in=SD, out=open
  not not_5 (not_5_out, TC2);
  not not_6 (not_6_out, TC3);
  and and_1 (and_1_out, not_1_out, Qb, Qc, KP, SD);
  and and_2 (and_2_out, Qa, not_2_out, not_3_out, KP, not_5_out, not_6_out);
  and and_3 (and_3_out, Qa, not_2_out, not_3_out, KP, SD, TC2, TC3);
  and and_4 (and_4_out, Qa, not_2_out, Qc, KP);
  or or_1 (out_8, and_1_out, and_2_out, and_3_out, and_4_out);
endmodule

module L2_LED2 (
  input  Qa,
  input  Qb,
  input  Qc,
  input  KP,
  input  SD,
  input  TC2,
  input  TC3,
  output out_8
);

  wire and_1_out, and_2_out, and_3_out, and_4_out, and_5_out, and_6_out, not_1_out, not_2_out, not_3_out,
       not_4_out, not_5_out, not_6_out;

  not not_1 (not_1_out, Qa);
  not not_2 (not_2_out, Qb);
  not not_3 (not_3_out, Qc);
  not not_4 (not_4_out, SD);
  not not_5 (not_5_out, TC2);
  not not_6 (not_6_out, TC3);
  and and_1 (and_1_out, not_1_out, not_2_out, Qc, KP, SD, TC2);
  and and_2 (and_2_out, not_1_out, not_2_out, Qc, KP, not_4_out, not_5_out);
  and and_3 (and_3_out, Qa, not_2_out, not_3_out, KP, not_4_out);
  and and_4 (and_4_out, Qa, not_2_out, not_3_out, KP, not_5_out, not_6_out);
  and and_5 (and_5_out, Qa, not_2_out, not_3_out, KP, SD, TC2, TC3);
  and and_6 (and_6_out, Qa, not_2_out, Qc, KP);
  or or_1 (out_8, and_1_out, and_2_out, and_3_out, and_4_out, and_5_out, and_6_out);
endmodule

module L2_LED3 (
  input  Qa,
  input  Qb,
  input  Qc,
  input  KP,
  output out_5
);

  wire not_2_out;

  // NOT_Gate not_1 has open pins: in=Qa, out=open
  not not_2 (not_2_out, Qb);
  // NOT_Gate not_3 has open pins: in=Qc, out=open
  and and_1 (out_5, Qa, not_2_out, Qc, KP);
endmodule

module L2_TA2 (
  input  Qa,
  input  Qb,
  input  Qc,
  input  KP,
  input  SD,
  input  TC2,
  input  TC3,
  output out_8
);

  wire and_1_out, and_2_out, and_3_out, and_4_out, and_5_out, not_1_out, not_2_out, not_3_out, not_4_out,
       not_5_out, not_6_out;

  not not_1 (not_1_out, Qa);
  not not_2 (not_2_out, Qb);
  not not_3 (not_3_out, Qc);
  not not_4 (not_4_out, SD);
  not not_5 (not_5_out, TC2);
  not not_6 (not_6_out, TC3);
  and and_1 (and_1_out, not_1_out, not_2_out, Qc, KP, SD, TC2);
  and and_2 (and_2_out, not_1_out, not_2_out, Qc, KP, not_4_out, not_5_out);
  and and_3 (and_3_out, Qa, not_2_out, not_3_out, KP, not_4_out);
  and and_4 (and_4_out, Qa, not_2_out, not_3_out, KP, not_5_out, not_6_out);
  and and_5 (and_5_out, Qa, not_2_out, not_3_out, KP, SD, TC2, TC3);
  or or_1 (out_8, and_1_out, and_2_out, and_3_out, and_4_out, and_5_out);
endmodule

module L2_TA3 (
  input  Qa,
  input  Qb,
  input  Qc,
  input  KP,
  input  SD,
  input  TC2,
  input  TC3,
  output out_8
);

  wire and_1_out, and_2_out, and_3_out, not_1_out, not_2_out, not_3_out, not_4_out, not_5_out;

  not not_1 (not_1_out, Qb);
  not not_2 (not_2_out, Qc);
  not not_3 (not_3_out, SD);
  not not_4 (not_4_out, TC2);
  not not_5 (not_5_out, TC3);
  and and_1 (and_1_out, Qa, not_1_out, not_2_out, KP, not_3_out);
  and and_2 (and_2_out, Qa, not_1_out, not_2_out, KP, not_4_out, not_5_out);
  and and_3 (and_3_out, Qa, not_1_out, not_2_out, KP, SD, TC2, TC3);
  or or_1 (out_8, and_1_out, and_2_out, and_3_out);
endmodule

module two_bit_counter (
  input  Clock,
  output [1:0] Count1
);

  Counter #(.max('h3), .width(2)) counter_1 (
    .load(1'b0), .count(1'b1), .Q(Count1), .up(1'b1), .clk(Clock), .clr(1'b0));  // open: D, carry
endmodule
