// Logisim project Sequence_Detector.circ as structural Verilog: 5 circuits, main circuit main
module main (
  input  Lock
);

  wire and_1_out, clock_1_out, d_ff_1_q, d_ff_2_q, d_ff_2_qn, d_ff_3_q, E1_out, E2_out, E3_out, E4_out,
       E5_out, edge_detector_1_out_3, edge_detector_2_out_3, edge_detector_3_out_3, edge_detector_4_out_3,
       edge_detector_5_out_3, qa_next_state_1_out_10, qb_next_state_1_out_10, qc_next_state_1_out_10;

  Clock clock_1 (.out(clock_1_out));
  Button E1 (.out(E1_out));
  Button E2 (.out(E2_out));
  Button E3 (.out(E3_out));
  Button E4 (.out(E4_out));
  Button E5 (.out(E5_out));
  edge_detector edge_detector_1 (.Input_Val(E1_out), .Clock(clock_1_out), .out_3(edge_detector_1_out_3));
  edge_detector edge_detector_2 (.Input_Val(E2_out), .Clock(clock_1_out), .out_3(edge_detector_2_out_3));
  edge_detector edge_detector_3 (.Input_Val(E3_out), .Clock(clock_1_out), .out_3(edge_detector_3_out_3));
  edge_detector edge_detector_4 (.Input_Val(E4_out), .Clock(clock_1_out), .out_3(edge_detector_4_out_3));
  edge_detector edge_detector_5 (.Input_Val(E5_out), .Clock(clock_1_out), .out_3(edge_detector_5_out_3));
  LED Qa (.in(d_ff_1_q));
  Qa_Next_State qa_next_state_1 (
    .Qa(d_ff_1_q), .Qb(d_ff_2_q), .Qc(d_ff_3_q), .E1(edge_detector_1_out_3), .E2(edge_detector_2_out_3),
    .E3(edge_detector_3_out_3), .E4(edge_detector_4_out_3), .E5(edge_detector_5_out_3), .Lock(Lock),
    .out_10(qa_next_state_1_out_10));
  Qb_Next_State qb_next_state_1 (
    .Qa(d_ff_1_q), .Qb(d_ff_2_q), .Qc(d_ff_3_q), .E1(edge_detector_1_out_3), .E2(edge_detector_2_out_3),
    .E3(edge_detector_3_out_3), .E4(edge_detector_4_out_3), .E5(edge_detector_5_out_3), .Lock(Lock),
    .out_10(qb_next_state_1_out_10));
  Qc_Next_State qc_next_state_1 (
    .Qa(d_ff_1_q), .Qb(d_ff_2_q), .Qc(d_ff_3_q), .E1(edge_detector_1_out_3), .E2(edge_detector_2_out_3),
    .E3(edge_detector_3_out_3), .E4(edge_detector_4_out_3), .E5(edge_detector_5_out_3), .Lock(Lock),
    .out_10(qc_next_state_1_out_10));
  LED Qc (.in(d_ff_3_q));
  LED Qb (.in(d_ff_2_q));
  D_Flip_Flop d_ff_1 (.D(qa_next_state_1_out_10), .clk(clock_1_out), .Q(d_ff_1_q));  // open: Qn, preset, reset
  D_Flip_Flop d_ff_2 (
    .D(qb_next_state_1_out_10), .clk(clock_1_out), .Q(d_ff_2_q), .Qn(d_ff_2_qn));  // open: preset, reset
  D_Flip_Flop d_ff_3 (.D(qc_next_state_1_out_10), .clk(clock_1_out), .Q(d_ff_3_q));  // open: Qn, preset, reset
  and and_1 (and_1_out, d_ff_1_q, d_ff_2_qn, d_ff_3_q);
  LED Unlocked (.in(and_1_out));
endmodule

module edge_detector (
  input  Input_Val,
  input  Clock,
  output out_3
);

  wire and_1_out, and_2_out, and_3_out, d_ff_1_q, d_ff_1_qn, d_ff_2_q, d_ff_2_qn, or_1_out, or_2_out;

  and and_1 (and_1_out, Input_Val, d_ff_2_q, d_ff_1_qn);
  and and_2 (and_2_out, Input_Val, d_ff_2_q, d_ff_1_q);
  and and_3 (and_3_out, d_ff_1_qn, Input_Val, d_ff_2_qn);
  or or_1 (or_1_out, and_1_out, out_3, and_2_out);
  or or_2 (or_2_out, and_2_out, out_3, and_3_out);
  D_Flip_Flop d_ff_1 (.D(or_1_out), .clk(Clock), .Q(d_ff_1_q), .Qn(d_ff_1_qn));  // open: preset, reset
  D_Flip_Flop d_ff_2 (.D(or_2_out), .clk(Clock), .Q(d_ff_2_q), .Qn(d_ff_2_qn));  // open: preset, reset
  and and_4 (out_3, d_ff_1_q, d_ff_2_qn);
endmodule

module Qc_Next_State (
  input  Qa,
  input  Qb,
  input  Qc,
  input  E1,
  input  E2,
  input  E3,
  input  E4,
  input  E5,
  input  Lock,
  output out_10
);

  wire and_1_out, and_2_out, and_3_out, and_4_out, and_5_out, and_6_out, not_1_out, not_2_out, not_3_out,
       not_4_out, not_5_out, not_6_out, not_7_out, not_8_out, not_9_out;

  not not_1 (not_1_out, Qa);
  not not_2 (not_2_out, Qb);
  not not_3 (not_3_out, Qc);
  not not_4 (not_4_out, E1);
  not not_5 (not_5_out, E2);
  not not_6 (not_6_out, E3);
  not not_7 (not_7_out, E4);
  not not_8 (not_8_out, E5);
  not not_9 (not_9_out, Lock);
  and and_1 (and_1_out, not_1_out, not_2_out, not_3_out, not_4_out, E2, not_6_out, not_7_out, not_8_out, not_9_out);
  and and_2 (and_2_out, not_1_out, not_2_out, Qc, not_4_out, not_5_out, not_6_out, not_7_out, not_8_out, not_9_out);
  and and_3 (and_3_out, not_1_out, Qb, not_3_out, not_4_out, not_5_out, E3, not_7_out, not_8_out, not_9_out);
  and and_4 (and_4_out, not_1_out, Qb, Qc, not_4_out, not_5_out, not_6_out, not_7_out, not_8_out, not_9_out);
  and and_5 (and_5_out, Qa, not_2_out, not_3_out, not_4_out, not_5_out, not_6_out, E4, not_8_out, not_9_out);
  and and_6 (and_6_out, Qa, not_2_out, Qc, not_4_out, not_9_out);
  or or_1 (out_10, and_1_out, and_2_out, and_3_out, and_4_out, and_5_out, and_6_out);
endmodule

module Qb_Next_State (
  input  Qa,
  input  Qb,
  input  Qc,
  input  E1,
  input  E2,
  input  E3,
  input  E4,
  input  E5,
  input  Lock,
  output out_10
);

  wire and_1_out, and_2_out, and_3_out, and_4_out, not_1_out, not_2_out, not_3_out, not_4_out, not_5_out,
       not_6_out, not_7_out, not_8_out, not_9_out;

  not not_1 (not_1_out, Qa);
  not not_2 (not_2_out, Qb);
  not not_3 (not_3_out, Qc);
  not not_4 (not_4_out, E1);
  not not_5 (not_5_out, E2);
  not not_6 (not_6_out, E3);
  not not_7 (not_7_out, E4);
  not not_8 (not_8_out, E5);
  not not_9 (not_9_out, Lock);
  and and_1 (and_1_out, not_1_out, not_2_out, Qc, not_4_out, not_5_out, not_6_out, not_7_out, E5, not_9_out);
  and and_2 (and_2_out, not_1_out, Qb, not_3_out, not_4_out, not_5_out, not_6_out, not_7_out, not_8_out, not_9_out);
  and and_3 (and_3_out, not_1_out, Qb, not_3_out, not_4_out, not_5_out, E3, not_7_out, not_8_out, not_9_out);
  and and_4 (and_4_out, not_1_out, Qb, Qb, not_4_out, not_5_out, not_6_out, not_7_out, not_8_out, not_9_out);
  or or_1 (out_10, and_1_out, and_2_out, and_3_out, and_4_out);
endmodule

module Qa_Next_State (
  input  Qa,
  input  Qb,
  input  Qc,
  input  E1,
  input  E2,
  input  E3,
  input  E4,
  input  E5,
  input  Lock,
  output out_10
);

  wire and_1_out, and_2_out, and_3_out, and_4_out, not_1_out, not_2_out, not_3_out, not_4_out, not_5_out,
       not_6_out, not_7_out, not_8_out, not_9_out;

  not not_1 (not_1_out, Qa);
  not not_2 (not_2_out, Qb);
  not not_3 (not_3_out, Qc);
  not not_4 (not_4_out, E1);
  not not_5 (not_5_out, E2);
  not not_6 (not_6_out, E3);
  not not_7 (not_7_out, E4);
  not not_8 (not_8_out, E5);
  not not_9 (not_9_out, Lock);
  and and_1 (and_1_out, not_1_out, Qb, Qc, E1, not_5_out, not_6_out, not_7_out, not_8_out, not_9_out);
  and and_2 (and_2_out, Qa, not_2_out, not_3_out, not_4_out, not_5_out, not_6_out, not_7_out, not_8_out, not_9_out);
  and and_3 (and_3_out, Qa, not_2_out, not_3_out, not_4_out, not_5_out, not_6_out, E4, not_8_out, not_9_out);
  and and_4 (and_4_out, Qa, not_2_out, Qc, not_4_out, not_9_out);
  or or_1 (out_10, and_1_out, and_2_out, and_3_out, and_4_out);
endmodule
