// Logisim project State_Machine_Introduction.circ as structural Verilog: 1 circuit, main circuit main
module main (
);

  wire and_1_out, and_2_out, and_3_out, button_1_out, clock_1_out, d_ff_1_q, d_ff_1_qn, d_ff_2_q, d_ff_2_qn,
       digital_oscilloscope_1_p3, or_1_out, or_2_out;

  Button button_1 (.out(button_1_out));
  Clock clock_1 (.out(clock_1_out));
  and and_1 (and_1_out, button_1_out, d_ff_2_q);
  and and_2 (and_2_out, d_ff_2_qn, button_1_out);
  and and_3 (and_3_out, d_ff_1_qn, d_ff_2_q, button_1_out);
  or or_1 (or_1_out, digital_oscilloscope_1_p3, and_1_out);
  or or_2 (or_2_out, digital_oscilloscope_1_p3, and_3_out, and_2_out);
  // Digital_Oscilloscope digital_oscilloscope_1: pin names not known; wires that end beside it: clock_1_out, button_1_out, digital_oscilloscope_1_p3
  D_Flip_Flop d_ff_1 (.D(or_1_out), .clk(clock_1_out), .Q(d_ff_1_q), .Qn(d_ff_1_qn));  // open: preset, reset
  D_Flip_Flop d_ff_2 (.D(or_2_out), .clk(clock_1_out), .Q(d_ff_2_q), .Qn(d_ff_2_qn));  // open: preset, reset
  and and_4 (digital_oscilloscope_1_p3, d_ff_1_q, d_ff_2_qn);
  LED led_1 (.in(digital_oscilloscope_1_p3));
endmodule
