// Logisim project Synchronous_Counter_P1.circ as structural Verilog: 2 circuits, main circuit main
module main (
  output Out_3,
  output Out_2,
  output Out_1,
  output Out_0
);

  wire and_1_out, and_2_out, clock_1_out, d_ff_4_qn, xor_1_out, xor_2_out, xor_3_out;

  Clock clock_1 (.out(clock_1_out));
  D_Flip_Flop d_ff_1 (.D(xor_1_out), .clk(clock_1_out), .Q(Out_3));  // open: Qn, preset, reset
  D_Flip_Flop d_ff_2 (.D(xor_2_out), .clk(clock_1_out), .Q(Out_2));  // open: Qn, preset, reset
  D_Flip_Flop d_ff_3 (.D(xor_3_out), .clk(clock_1_out), .Q(Out_1));  // open: Qn, preset, reset
  and and_1 (and_1_out, Out_2, Out_0, Out_1);
  and and_2 (and_2_out, Out_0, Out_1);
  D_Flip_Flop d_ff_4 (.D(d_ff_4_qn), .clk(clock_1_out), .Q(Out_0), .Qn(d_ff_4_qn));  // open: preset, reset
  xor xor_1 (xor_1_out, Out_3, and_1_out);
  xor xor_2 (xor_2_out, Out_2, and_2_out);
  xor xor_3 (xor_3_out, Out_1, Out_0);
endmodule

module Graph (
);

  wire and_1_out, and_2_out, clock_1_out, d_ff_1_q, d_ff_2_q, d_ff_3_q, d_ff_4_q, d_ff_4_qn, xor_1_out,
       xor_2_out, xor_3_out;

  Clock clock_1 (.out(clock_1_out));
  D_Flip_Flop d_ff_1 (.D(xor_1_out), .clk(clock_1_out), .Q(d_ff_1_q));  // open: Qn, preset, reset
  D_Flip_Flop d_ff_2 (.D(xor_2_out), .clk(clock_1_out), .Q(d_ff_2_q));  // open: Qn, preset, reset
  D_Flip_Flop d_ff_3 (.D(xor_3_out), .clk(clock_1_out), .Q(d_ff_3_q));  // open: Qn, preset, reset
  and and_1 (and_1_out, d_ff_2_q, d_ff_4_q, d_ff_3_q);
  and and_2 (and_2_out, d_ff_4_q, d_ff_3_q);
  D_Flip_Flop d_ff_4 (.D(d_ff_4_qn), .clk(clock_1_out), .Q(d_ff_4_q), .Qn(d_ff_4_qn));  // open: preset, reset
  xor xor_1 (xor_1_out, d_ff_1_q, and_1_out);
  xor xor_2 (xor_2_out, d_ff_2_q, and_2_out);
  xor xor_3 (xor_3_out, d_ff_3_q, d_ff_4_q);
  // Digital_Oscilloscope digital_oscilloscope_1: pin names not known; wires that end beside it: d_ff_4_qn, d_ff_4_q, d_ff_3_q, d_ff_2_q, d_ff_1_q
endmodule
